// Logisim project 8_Bit_Computer_Final.circ as structural Verilog: 13 circuits, main circuit main
module main (
  input  CLK_ENB,
  input  MAR_OUT,
  input  PROGRAM_MODE,
  input  BO
);

  wire A_IN, A_OUT, alu_1_c_out, ALU_OUT, B_IN, CF, clk_1_clk_out, clock_1_out, COUNTER_ENB, COUNTER_OUT,
       decoder_1_out0, decoder_1_out1, decoder_1_out2, decoder_1_out3, decoder_1_out4, decoder_1_out5,
       FLAGS_IN, HALT, INR_IN, INR_OUT, JUMP, MANUAL_TICK_out, MAR_IN, multiplexer_2_out,
       n7_segment_display_1_p1, n7_segment_display_2_p1, n7_segment_display_3_p1, not_1_out, not_2_out,
       or_1_out, or_2_out, OUTPUT_REG_IN, RAM_IN, RAM_OUT, RESET_out, SUB, zero_flag_1_zero, ZF;
  wire [2:0] step_counter_1_binary_out;
  wire [3:0] dipswitch_1_sw4, mar_1_always_out, multiplexer_3_out;
  wire [7:0] a_register_1_always_out, alu_1_always_out, b_register_1_always_out, dipswitch_2_sw8,
       ir_1_always_out, mar_1_data_out, multiplexer_1_out, output_register_1_data_out;

  Button RESET (.out(RESET_out));
  Clock clock_1 (.out(clock_1_out));
  Button MANUAL_TICK (.out(MANUAL_TICK_out));
  DipSwitch #(.number(4)) dipswitch_1 (
    .sw1(dipswitch_1_sw4[3]), .sw2(dipswitch_1_sw4[2]), .sw3(dipswitch_1_sw4[1]), .sw4(dipswitch_1_sw4[0]));
  DipSwitch dipswitch_2 (
    .sw1(dipswitch_2_sw8[7]), .sw2(dipswitch_2_sw8[6]), .sw3(dipswitch_2_sw8[5]), .sw4(dipswitch_2_sw8[4]),
    .sw5(dipswitch_2_sw8[3]), .sw6(dipswitch_2_sw8[2]), .sw7(dipswitch_2_sw8[1]), .sw8(dipswitch_2_sw8[0]));
  or or_1 (or_1_out, RESET_out, decoder_1_out5);
  LED led_1 (.in(not_1_out));
  LED led_2 (.in(PROGRAM_MODE));
  not not_1 (not_1_out, PROGRAM_MODE);
  not not_2 (not_2_out, clk_1_clk_out);
  or or_2 (or_2_out, or_1_out, PROGRAM_MODE);
  Multiplexer #(.width(8)) multiplexer_1 (
    .in0(mar_1_data_out), .in1(dipswitch_2_sw8), .out(multiplexer_1_out), .sel(PROGRAM_MODE));
  Multiplexer multiplexer_2 (.in0(RAM_IN), .in1(PROGRAM_MODE), .out(multiplexer_2_out), .sel(PROGRAM_MODE));
  Step_Counter step_counter_1 (.RESET(or_2_out), .CLOCK(not_2_out), .BINARY_OUT(step_counter_1_binary_out));
  Decoder #(.select(3)) decoder_1 (
    .out0(decoder_1_out0), .out1(decoder_1_out1), .out2(decoder_1_out2), .out3(decoder_1_out3),
    .out4(decoder_1_out4), .out5(decoder_1_out5), .sel(step_counter_1_binary_out));  // open: out6, out7, en
  LED T0 (.in(decoder_1_out0));
  LED T1 (.in(decoder_1_out1));
  ROM #(.addrWidth(9), .dataWidth(16)) rom_1 (
    .addr({ZF, CF, ir_1_always_out[7:4], step_counter_1_binary_out}),
    .data({HALT, MAR_IN, RAM_IN, RAM_OUT, INR_OUT, INR_IN, A_IN, A_OUT, ALU_OUT, SUB, B_IN, OUTPUT_REG_IN, COUNTER_ENB, COUNTER_OUT, JUMP, FLAGS_IN}));
  Multiplexer #(.width(4)) multiplexer_3 (
    .in0(mar_1_always_out), .in1(dipswitch_1_sw4), .out(multiplexer_3_out), .sel(PROGRAM_MODE));
  LED T2 (.in(decoder_1_out2));
  LED T3 (.in(decoder_1_out3));
  LED T4 (.in(decoder_1_out4));
  CLK clk_1 (
    .HALT(HALT), .CLK_IN(clock_1_out), .CLK_ENABLE(CLK_ENB), .MANUAL_CLK(MANUAL_TICK_out),
    .CLK_OUT(clk_1_clk_out));
  MAR mar_1 (
    .MAR_IN(MAR_IN), .CLOCK(clk_1_clk_out), .MAR_RESET(RESET_out), .MAR_OUT(MAR_OUT),
    .DATA_IN(mar_1_data_out[3:0]), .ALWAYS_OUT(mar_1_always_out), .DATA_OUT(mar_1_data_out[3:0]));
  MEMORY memory_1 (
    .RAM_OUT_ENB(RAM_OUT), .STORE(multiplexer_2_out), .CLOCK(clk_1_clk_out), .ADDRESS(multiplexer_3_out),
    .DATA(multiplexer_1_out), .RAM_OUT(mar_1_data_out));
  IR ir_1 (
    .DATA_OUT_ENABLE(INR_OUT), .DATA_IN(mar_1_data_out), .STORE(INR_IN), .CLOCK(clk_1_clk_out),
    .RESET(RESET_out), .ALWAYS_OUT(ir_1_always_out), .DATA_OUT(mar_1_data_out));
  LED led_3 (.in(mar_1_data_out[7]));
  LED led_4 (.in(mar_1_data_out[6]));
  LED led_5 (.in(mar_1_data_out[5]));
  Pull_Resistor pull_resistor_1 (.node(mar_1_data_out[7]));
  Pull_Resistor pull_resistor_2 (.node(mar_1_data_out[6]));
  Pull_Resistor pull_resistor_3 (.node(mar_1_data_out[5]));
  LED led_6 (.in(mar_1_data_out[4]));
  LED led_7 (.in(mar_1_data_out[3]));
  LED led_8 (.in(mar_1_data_out[2]));
  LED led_9 (.in(mar_1_data_out[1]));
  Pull_Resistor pull_resistor_4 (.node(mar_1_data_out[4]));
  Pull_Resistor pull_resistor_5 (.node(mar_1_data_out[3]));
  Pull_Resistor pull_resistor_6 (.node(mar_1_data_out[2]));
  Pull_Resistor pull_resistor_7 (.node(mar_1_data_out[1]));
  LED led_10 (.in(mar_1_data_out[0]));
  Pull_Resistor pull_resistor_8 (.node(mar_1_data_out[0]));
  PC pc_1 (
    .RESET(RESET_out), .JUMP(JUMP), .COUNTER_ENABLE(COUNTER_ENB), .CLOCK(clk_1_clk_out),
    .COUNTER_OUT(COUNTER_OUT), .ADDRESS_IN(mar_1_data_out[3:0]), .ADDRESS_OUT(mar_1_data_out[3:0]));  // open: ALWAYS_OUT
  OUTPUT_Register output_register_1 (
    .STORE(OUTPUT_REG_IN), .CLOCK(clk_1_clk_out), .RESET(RESET_out), .DATA_IN(mar_1_data_out),
    .DATA_OUT(output_register_1_data_out));
  // _7_Segment_Display 7_segment_display_1: pin names not known; wires that end beside it: n7_segment_display_1_p1, n7_segment_display_1_p1
  // BCD_to_7_Segment_decoder bcd_to_7_segment_decoder_1: pin names not known
  // Binary_to_BCD_converter #(.binvalue(8)) binary_to_bcd_converter_1: pin names not known; wires that end beside it: output_register_1_data_out
  LED HLT (.in(HALT));
  LED MI (.in(MAR_IN));
  LED RI (.in(RAM_IN));
  LED RO (.in(RAM_OUT));
  A_Register a_register_1 (
    .A_IN(A_IN), .A_OUT(A_OUT), .CLOCK(clk_1_clk_out), .A_RESET(RESET_out), .DATA_IN(mar_1_data_out),
    .ALWAYS_OUT(a_register_1_always_out), .DATA_OUT(mar_1_data_out));
  ALU alu_1 (
    .A_IN(a_register_1_always_out), .B_IN(b_register_1_always_out), .OUTPUT_ENB(ALU_OUT), .SUB(SUB),
    .ALWAYS_OUT(alu_1_always_out), .ALU_DATA_OUT(mar_1_data_out), .C_OUT(alu_1_c_out));
  B_Register b_register_1 (
    .B_IN(B_IN), .B_OUT(BO), .CLOCK(clk_1_clk_out), .B_RESET(RESET_out), .DATA_IN(mar_1_data_out),
    .ALWAYS_OUT(b_register_1_always_out), .DATA_OUT(mar_1_data_out));
  // _7_Segment_Display 7_segment_display_2: pin names not known; wires that end beside it: n7_segment_display_2_p1, n7_segment_display_2_p1
  // _7_Segment_Display 7_segment_display_3: pin names not known; wires that end beside it: n7_segment_display_3_p1, n7_segment_display_3_p1
  // BCD_to_7_Segment_decoder bcd_to_7_segment_decoder_2: pin names not known
  // BCD_to_7_Segment_decoder bcd_to_7_segment_decoder_3: pin names not known
  LED IO (.in(INR_OUT));
  LED II (.in(INR_IN));
  LED AI (.in(A_IN));
  LED A0 (.in(A_OUT));
  Zero_Flag zero_flag_1 (.in_1(alu_1_always_out), .ZERO(zero_flag_1_zero));
  FLAGS flags_1 (
    .CARRY(alu_1_c_out), .ZERO(zero_flag_1_zero), .STORE(FLAGS_IN), .CLOCK(clk_1_clk_out), .RESET(RESET_out),
    .CARRY_OUT(CF), .ZERO_OUT(ZF));
  LED BI (.in(B_IN));
  LED OI (.in(OUTPUT_REG_IN));
  LED EO (.in(ALU_OUT));
  LED SU (.in(SUB));
  LED CE (.in(COUNTER_ENB));
  LED CO (.in(COUNTER_OUT));
  LED J (.in(JUMP));
  LED led_11 (.in(FLAGS_IN));

  // Notes on the sheet:
  //   ADDRESS
  //   DATA
  //   contents of rom_1 (hex, n*v repeats v):
  //   4004 1408 6*0 4004 1408 4800 1200 4*0 4004 1408 4800 1020 281 0 0 0 4004 1408 4800 1020 2c1 0 0 0
  //   4004 1408 4800 2100 4*0 4004 1408 a00 5*0 4004 1408 802 5*0 4004 1408 6*0 4004 1408 6*0 4004 1408
  //   6*0 4004 1408 6*0 4004 1408 6*0 4004 1408 6*0 4004 1408 6*0 4004 1408 110 5*0 4004 1408 8000 5*0
  //   4004 1408 6*0 4004 1408 4800 1200 4*0 4004 1408 4800 1020 281 0 0 0 4004 1408 4800 1020 2c1 0 0 0
  //   4004 1408 4800 2100 4*0 4004 1408 a00 5*0 4004 1408 802 5*0 4004 1408 802 5*0 4004 1408 6*0 4004
  //   1408 6*0 4004 1408 6*0 4004 1408 6*0 4004 1408 6*0 4004 1408 6*0 4004 1408 110 5*0 4004 1408 8000
  //   5*0 4004 1408 6*0 4004 1408 4800 1200 4*0 4004 1408 4800 1020 281 0 0 0 4004 1408 4800 1020 2c1 0 0
  //   0 4004 1408 4800 2100 4*0 4004 1408 a00 5*0 4004 1408 802 5*0 4004 1408 6*0 4004 1408 802 5*0 4004
  //   1408 6*0 4004 1408 6*0 4004 1408 6*0 4004 1408 6*0 4004 1408 6*0 4004 1408 110 5*0 4004 1408 8000
  //   5*0 4004 1408 6*0 4004 1408 4800 1200 4*0 4004 1408 4800 1020 281 0 0 0 4004 1408 4800 1020 2c1 0 0
  //   0 4004 1408 4800 2100 4*0 4004 1408 a00 5*0 4004 1408 802 5*0 4004 1408 802 5*0 4004 1408 802 5*0
  //   4004 1408 6*0 4004 1408 6*0 4004 1408 6*0 4004 1408 6*0 4004 1408 6*0 4004 1408 110 5*0 4004 1408
  //   8000
endmodule

module CLK (
  input  CLK_IN,
  input  CLK_ENABLE,
  input  MANUAL_CLK,
  input  HALT,
  output CLK_OUT
);

  wire and_1_out, and_2_out, not_1_out, not_2_out, or_1_out;

  not not_1 (not_1_out, CLK_ENABLE);
  not not_2 (not_2_out, HALT);
  and and_1 (and_1_out, CLK_IN, CLK_ENABLE);
  and and_2 (and_2_out, not_1_out, MANUAL_CLK);
  or or_1 (or_1_out, and_1_out, and_2_out);
  and and_3 (CLK_OUT, or_1_out, not_2_out);
endmodule

module PC (
  input  RESET,
  input  JUMP,
  input  COUNTER_ENABLE,
  input  CLOCK,
  input  [3:0] ADDRESS_IN,
  input  COUNTER_OUT,
  output [3:0] ALWAYS_OUT,
  output [3:0] ADDRESS_OUT
);

  Counter #(.max('hf), .width(4)) counter_1 (
    .clr(RESET), .load(JUMP), .up(COUNTER_ENABLE), .count(COUNTER_ENABLE), .clk(CLOCK), .D(ADDRESS_IN),
    .Q(ALWAYS_OUT));  // open: carry
  LED led_1 (.in(ALWAYS_OUT[3]));
  LED led_2 (.in(ALWAYS_OUT[2]));
  LED led_3 (.in(ALWAYS_OUT[1]));
  LED led_4 (.in(ALWAYS_OUT[0]));
  assign ADDRESS_OUT = COUNTER_OUT ? ALWAYS_OUT : 4'bz;  // Controlled_Buffer controlled_buffer_1
  Pull_Resistor pull_resistor_1 (.node(ALWAYS_OUT[0]));
  Pull_Resistor pull_resistor_2 (.node(ALWAYS_OUT[1]));
  Pull_Resistor pull_resistor_3 (.node(ALWAYS_OUT[2]));
  Pull_Resistor pull_resistor_4 (.node(ALWAYS_OUT[3]));
endmodule

module A_Register (
  input  [7:0] DATA_IN,
  input  A_IN,
  input  A_OUT,
  input  CLOCK,
  input  A_RESET,
  output [7:0] ALWAYS_OUT,
  output [7:0] DATA_OUT
);

  Register register_1 (.D(DATA_IN), .en(A_IN), .clk(CLOCK), .Q(ALWAYS_OUT), .clr(A_RESET));
  LED led_1 (.in(ALWAYS_OUT[7]));
  LED led_2 (.in(ALWAYS_OUT[6]));
  LED led_3 (.in(ALWAYS_OUT[5]));
  LED led_4 (.in(ALWAYS_OUT[2]));
  LED led_5 (.in(ALWAYS_OUT[1]));
  LED led_6 (.in(ALWAYS_OUT[4]));
  LED led_7 (.in(ALWAYS_OUT[3]));
  LED led_8 (.in(ALWAYS_OUT[0]));
  assign DATA_OUT = A_OUT ? ALWAYS_OUT : 8'bz;  // Controlled_Buffer controlled_buffer_1
  Pull_Resistor pull_resistor_1 (.node(ALWAYS_OUT[0]));
  Pull_Resistor pull_resistor_2 (.node(ALWAYS_OUT[1]));
  Pull_Resistor pull_resistor_3 (.node(ALWAYS_OUT[2]));
  Pull_Resistor pull_resistor_4 (.node(ALWAYS_OUT[3]));
  Pull_Resistor pull_resistor_5 (.node(ALWAYS_OUT[4]));
  Pull_Resistor pull_resistor_6 (.node(ALWAYS_OUT[5]));
  Pull_Resistor pull_resistor_7 (.node(ALWAYS_OUT[6]));
  Pull_Resistor pull_resistor_8 (.node(ALWAYS_OUT[7]));
endmodule

module ALU (
  input  [7:0] A_IN,
  input  [7:0] B_IN,
  input  OUTPUT_ENB,
  input  SUB,
  output [7:0] ALWAYS_OUT,
  output [7:0] ALU_DATA_OUT,
  output C_OUT
);

  wire not_1_out;
  wire [7:0] controlled_buffer_1_out, xor_1_out;

  assign controlled_buffer_1_out = SUB ? {8{1'b1}} : 8'bz;  // Controlled_Buffer controlled_buffer_1
  assign controlled_buffer_1_out = not_1_out ? {8{1'b0}} : 8'bz;  // Controlled_Buffer controlled_buffer_2
  not not_1 (not_1_out, SUB);
  assign xor_1_out = B_IN ^ controlled_buffer_1_out;  // XOR_Gate xor_1, 8 bits wide
  LED led_1 (.in(ALWAYS_OUT[7]));
  LED led_2 (.in(ALWAYS_OUT[6]));
  Adder adder_1 (.a(A_IN), .b(xor_1_out), .out(ALWAYS_OUT), .cin(SUB), .cout(C_OUT));
  LED led_3 (.in(ALWAYS_OUT[5]));
  LED led_4 (.in(ALWAYS_OUT[4]));
  LED led_5 (.in(ALWAYS_OUT[3]));
  LED led_6 (.in(ALWAYS_OUT[2]));
  LED led_7 (.in(ALWAYS_OUT[1]));
  LED led_8 (.in(ALWAYS_OUT[0]));
  assign ALU_DATA_OUT = OUTPUT_ENB ? ALWAYS_OUT : 8'bz;  // Controlled_Buffer controlled_buffer_3
  Pull_Resistor pull_resistor_1 (.node(ALWAYS_OUT[0]));
  Pull_Resistor pull_resistor_2 (.node(ALWAYS_OUT[1]));
  Pull_Resistor pull_resistor_3 (.node(ALWAYS_OUT[2]));
  Pull_Resistor pull_resistor_4 (.node(ALWAYS_OUT[3]));
  Pull_Resistor pull_resistor_5 (.node(ALWAYS_OUT[4]));
  Pull_Resistor pull_resistor_6 (.node(ALWAYS_OUT[5]));
  Pull_Resistor pull_resistor_7 (.node(ALWAYS_OUT[6]));
  Pull_Resistor pull_resistor_8 (.node(ALWAYS_OUT[7]));
endmodule

module B_Register (
  input  [7:0] DATA_IN,
  input  B_IN,
  input  B_OUT,
  input  CLOCK,
  input  B_RESET,
  output [7:0] ALWAYS_OUT,
  output [7:0] DATA_OUT
);

  Register register_1 (.D(DATA_IN), .en(B_IN), .clk(CLOCK), .Q(ALWAYS_OUT), .clr(B_RESET));
  LED led_1 (.in(ALWAYS_OUT[7]));
  LED led_2 (.in(ALWAYS_OUT[6]));
  LED led_3 (.in(ALWAYS_OUT[5]));
  LED led_4 (.in(ALWAYS_OUT[2]));
  LED led_5 (.in(ALWAYS_OUT[1]));
  LED led_6 (.in(ALWAYS_OUT[4]));
  LED led_7 (.in(ALWAYS_OUT[3]));
  LED led_8 (.in(ALWAYS_OUT[0]));
  assign DATA_OUT = B_OUT ? ALWAYS_OUT : 8'bz;  // Controlled_Buffer controlled_buffer_1
  Pull_Resistor pull_resistor_1 (.node(ALWAYS_OUT[0]));
  Pull_Resistor pull_resistor_2 (.node(ALWAYS_OUT[1]));
  Pull_Resistor pull_resistor_3 (.node(ALWAYS_OUT[2]));
  Pull_Resistor pull_resistor_4 (.node(ALWAYS_OUT[3]));
  Pull_Resistor pull_resistor_5 (.node(ALWAYS_OUT[4]));
  Pull_Resistor pull_resistor_6 (.node(ALWAYS_OUT[5]));
  Pull_Resistor pull_resistor_7 (.node(ALWAYS_OUT[6]));
  Pull_Resistor pull_resistor_8 (.node(ALWAYS_OUT[7]));
endmodule

module OUTPUT_Register (
  input  [7:0] DATA_IN,
  input  STORE,
  input  CLOCK,
  input  RESET,
  output [7:0] DATA_OUT
);

  Register register_1 (.D(DATA_IN), .en(STORE), .clk(CLOCK), .Q(DATA_OUT), .clr(RESET));
endmodule

module MAR (
  input  [3:0] DATA_IN,
  input  MAR_IN,
  input  CLOCK,
  input  MAR_RESET,
  input  MAR_OUT,
  output [3:0] ALWAYS_OUT,
  output [3:0] DATA_OUT
);

  Register #(.width(4)) register_1 (.D(DATA_IN), .en(MAR_IN), .clk(CLOCK), .Q(ALWAYS_OUT), .clr(MAR_RESET));
  LED led_1 (.in(ALWAYS_OUT[3]));
  LED led_2 (.in(ALWAYS_OUT[2]));
  LED led_3 (.in(ALWAYS_OUT[1]));
  LED led_4 (.in(ALWAYS_OUT[0]));
  assign DATA_OUT = MAR_OUT ? ALWAYS_OUT : 4'bz;  // Controlled_Buffer controlled_buffer_1
  Pull_Resistor pull_resistor_1 (.node(ALWAYS_OUT[0]));
  Pull_Resistor pull_resistor_2 (.node(ALWAYS_OUT[1]));
  Pull_Resistor pull_resistor_3 (.node(ALWAYS_OUT[2]));
  Pull_Resistor pull_resistor_4 (.node(ALWAYS_OUT[3]));
endmodule

module MEMORY (
  input  [7:0] DATA,
  input  STORE,
  input  CLOCK,
  input  [3:0] ADDRESS,
  input  RAM_OUT_ENB,
  output [7:0] RAM_OUT
);

  wire and_1_out, and_2_out, and_3_out, and_4_out, and_5_out, and_6_out, and_7_out, and_8_out, and_9_out,
       and_10_out, and_11_out, and_12_out, and_13_out, and_14_out, and_15_out, and_16_out, decoder_1_out0,
       decoder_1_out1, decoder_1_out2, decoder_1_out3, decoder_1_out4, decoder_1_out5, decoder_1_out6,
       decoder_1_out7, decoder_1_out8, decoder_1_out9, decoder_1_out10, decoder_1_out11, decoder_1_out12,
       decoder_1_out13, decoder_1_out14, decoder_1_out15;
  wire [7:0] demultiplexer_1_out0, demultiplexer_1_out1, demultiplexer_1_out2, demultiplexer_1_out3,
       demultiplexer_1_out4, demultiplexer_1_out5, demultiplexer_1_out6, demultiplexer_1_out7,
       demultiplexer_1_out8, demultiplexer_1_out9, demultiplexer_1_out10, demultiplexer_1_out11,
       demultiplexer_1_out12, demultiplexer_1_out13, demultiplexer_1_out14, demultiplexer_1_out15,
       multiplexer_1_out, register_1_q, register_2_q, register_3_q, register_4_q, register_5_q, register_6_q,
       register_7_q, register_8_q, register_9_q, register_10_q, register_11_q, register_12_q, register_13_q,
       register_14_q, register_15_q, register_16_q;

  Pull_Resistor pull_resistor_1 (.node(ADDRESS[0]));
  Pull_Resistor pull_resistor_2 (.node(ADDRESS[1]));
  Pull_Resistor pull_resistor_3 (.node(ADDRESS[2]));
  Pull_Resistor pull_resistor_4 (.node(ADDRESS[3]));
  LED led_1 (.in(ADDRESS[3]));
  LED led_2 (.in(ADDRESS[2]));
  LED led_3 (.in(ADDRESS[1]));
  LED led_4 (.in(ADDRESS[0]));
  Decoder #(.select(4)) decoder_1 (
    .out0(decoder_1_out0), .out1(decoder_1_out1), .out2(decoder_1_out2), .out3(decoder_1_out3),
    .out4(decoder_1_out4), .out5(decoder_1_out5), .out6(decoder_1_out6), .out7(decoder_1_out7),
    .out8(decoder_1_out8), .out9(decoder_1_out9), .out10(decoder_1_out10), .out11(decoder_1_out11),
    .out12(decoder_1_out12), .out13(decoder_1_out13), .out14(decoder_1_out14), .out15(decoder_1_out15),
    .sel(ADDRESS));  // open: en
  Demultiplexer #(.select(4), .width(8)) demultiplexer_1 (
    .out0(demultiplexer_1_out0), .out1(demultiplexer_1_out1), .out2(demultiplexer_1_out2),
    .out3(demultiplexer_1_out3), .out4(demultiplexer_1_out4), .out5(demultiplexer_1_out5),
    .out6(demultiplexer_1_out6), .out7(demultiplexer_1_out7), .out8(demultiplexer_1_out8),
    .out9(demultiplexer_1_out9), .out10(demultiplexer_1_out10), .out11(demultiplexer_1_out11),
    .out12(demultiplexer_1_out12), .out13(demultiplexer_1_out13), .out14(demultiplexer_1_out14),
    .out15(demultiplexer_1_out15), .in(DATA), .sel(ADDRESS));
  and and_1 (and_1_out, decoder_1_out0, STORE);
  and and_2 (and_2_out, decoder_1_out1, STORE);
  and and_3 (and_3_out, decoder_1_out2, STORE);
  and and_4 (and_4_out, decoder_1_out3, STORE);
  and and_5 (and_5_out, decoder_1_out4, STORE);
  and and_6 (and_6_out, decoder_1_out5, STORE);
  and and_7 (and_7_out, decoder_1_out6, STORE);
  and and_8 (and_8_out, decoder_1_out7, STORE);
  and and_9 (and_9_out, decoder_1_out8, STORE);
  and and_10 (and_10_out, decoder_1_out9, STORE);
  and and_11 (and_11_out, decoder_1_out10, STORE);
  and and_12 (and_12_out, decoder_1_out11, STORE);
  and and_13 (and_13_out, decoder_1_out12, STORE);
  and and_14 (and_14_out, decoder_1_out13, STORE);
  and and_15 (and_15_out, decoder_1_out14, STORE);
  and and_16 (and_16_out, decoder_1_out15, STORE);
  Register register_1 (.D(demultiplexer_1_out0), .en(and_1_out), .clk(CLOCK), .Q(register_1_q));  // open: clr
  Register register_2 (.D(demultiplexer_1_out1), .en(and_2_out), .clk(CLOCK), .Q(register_2_q));  // open: clr
  Register register_3 (.D(demultiplexer_1_out2), .en(and_3_out), .clk(CLOCK), .Q(register_3_q));  // open: clr
  Register register_4 (.D(demultiplexer_1_out3), .en(and_4_out), .clk(CLOCK), .Q(register_4_q));  // open: clr
  Register register_5 (.D(demultiplexer_1_out4), .en(and_5_out), .clk(CLOCK), .Q(register_5_q));  // open: clr
  Register register_6 (.D(demultiplexer_1_out5), .en(and_6_out), .clk(CLOCK), .Q(register_6_q));  // open: clr
  Register register_7 (.D(demultiplexer_1_out6), .en(and_7_out), .clk(CLOCK), .Q(register_7_q));  // open: clr
  Register register_8 (.D(demultiplexer_1_out7), .en(and_8_out), .clk(CLOCK), .Q(register_8_q));  // open: clr
  Register register_9 (.D(demultiplexer_1_out8), .en(and_9_out), .clk(CLOCK), .Q(register_9_q));  // open: clr
  Register register_10 (.D(demultiplexer_1_out9), .en(and_10_out), .clk(CLOCK), .Q(register_10_q));  // open: clr
  Register register_11 (.D(demultiplexer_1_out10), .en(and_11_out), .clk(CLOCK), .Q(register_11_q));  // open: clr
  Register register_12 (.D(demultiplexer_1_out11), .en(and_12_out), .clk(CLOCK), .Q(register_12_q));  // open: clr
  Register register_13 (.D(demultiplexer_1_out12), .en(and_13_out), .clk(CLOCK), .Q(register_13_q));  // open: clr
  Register register_14 (.D(demultiplexer_1_out13), .en(and_14_out), .clk(CLOCK), .Q(register_14_q));  // open: clr
  Register register_15 (.D(demultiplexer_1_out14), .en(and_15_out), .clk(CLOCK), .Q(register_15_q));  // open: clr
  Register register_16 (.D(demultiplexer_1_out15), .en(and_16_out), .clk(CLOCK), .Q(register_16_q));  // open: clr
  Multiplexer #(.select(4), .width(8)) multiplexer_1 (
    .in0(register_1_q), .in1(register_2_q), .in2(register_3_q), .in3(register_4_q), .in4(register_5_q),
    .in5(register_6_q), .in6(register_7_q), .in7(register_8_q), .in8(register_9_q), .in9(register_10_q),
    .in10(register_11_q), .in11(register_12_q), .in12(register_13_q), .in13(register_14_q),
    .in14(register_15_q), .in15(register_16_q), .out(multiplexer_1_out), .sel(ADDRESS));
  LED led_5 (.in(multiplexer_1_out[7]));
  LED led_6 (.in(multiplexer_1_out[6]));
  LED led_7 (.in(multiplexer_1_out[5]));
  LED led_8 (.in(multiplexer_1_out[4]));
  assign RAM_OUT = RAM_OUT_ENB ? multiplexer_1_out : 8'bz;  // Controlled_Buffer controlled_buffer_1
  LED led_9 (.in(multiplexer_1_out[3]));
  LED led_10 (.in(multiplexer_1_out[2]));
  LED led_11 (.in(multiplexer_1_out[1]));
  LED led_12 (.in(multiplexer_1_out[0]));
  Pull_Resistor pull_resistor_5 (.node(multiplexer_1_out[0]));
  Pull_Resistor pull_resistor_6 (.node(multiplexer_1_out[1]));
  Pull_Resistor pull_resistor_7 (.node(multiplexer_1_out[2]));
  Pull_Resistor pull_resistor_8 (.node(multiplexer_1_out[3]));
  Pull_Resistor pull_resistor_9 (.node(multiplexer_1_out[4]));
  Pull_Resistor pull_resistor_10 (.node(multiplexer_1_out[5]));
  Pull_Resistor pull_resistor_11 (.node(multiplexer_1_out[6]));
  Pull_Resistor pull_resistor_12 (.node(multiplexer_1_out[7]));
endmodule

module IR (
  input  [7:0] DATA_IN,
  input  STORE,
  input  CLOCK,
  input  RESET,
  input  DATA_OUT_ENABLE,
  output [7:0] ALWAYS_OUT,
  output [7:0] DATA_OUT
);

  wire [7:4] pull_resistor_1_node;

  Register register_1 (.D(DATA_IN), .en(STORE), .clk(CLOCK), .Q(ALWAYS_OUT), .clr(RESET));
  LED led_1 (.in(ALWAYS_OUT[7]));
  LED led_2 (.in(ALWAYS_OUT[6]));
  LED led_3 (.in(ALWAYS_OUT[5]));
  LED led_4 (.in(ALWAYS_OUT[4]));
  LED led_5 (.in(ALWAYS_OUT[3]));
  LED led_6 (.in(ALWAYS_OUT[2]));
  LED led_7 (.in(ALWAYS_OUT[1]));
  Pull_Resistor pull_resistor_1 (.node(pull_resistor_1_node[4]));
  Pull_Resistor pull_resistor_2 (.node(pull_resistor_1_node[5]));
  Pull_Resistor pull_resistor_3 (.node(pull_resistor_1_node[6]));
  Pull_Resistor pull_resistor_4 (.node(pull_resistor_1_node[7]));
  LED led_8 (.in(ALWAYS_OUT[0]));
  assign DATA_OUT = DATA_OUT_ENABLE ? {pull_resistor_1_node, ALWAYS_OUT[3:0]} : 8'bz;  // Controlled_Buffer controlled_buffer_1
  Pull_Resistor pull_resistor_5 (.node(ALWAYS_OUT[0]));
  Pull_Resistor pull_resistor_6 (.node(ALWAYS_OUT[1]));
  Pull_Resistor pull_resistor_7 (.node(ALWAYS_OUT[2]));
  Pull_Resistor pull_resistor_8 (.node(ALWAYS_OUT[3]));
  Pull_Resistor pull_resistor_9 (.node(ALWAYS_OUT[4]));
  Pull_Resistor pull_resistor_10 (.node(ALWAYS_OUT[5]));
  Pull_Resistor pull_resistor_11 (.node(ALWAYS_OUT[6]));
  Pull_Resistor pull_resistor_12 (.node(ALWAYS_OUT[7]));
endmodule

module Step_Counter (
  input  RESET,
  input  CLOCK,
  output [2:0] BINARY_OUT
);

  wire pull_resistor_1_node, pull_resistor_2_node, pull_resistor_3_node;

  Counter #(.max('h5), .width(3)) counter_1 (
    .clr(RESET), .up(1'b1), .count(1'b1), .clk(CLOCK), .Q(BINARY_OUT));  // open: load, D, carry
  LED led_1 (.in(BINARY_OUT[2]));
  LED led_2 (.in(BINARY_OUT[1]));
  LED led_3 (.in(BINARY_OUT[0]));
  Pull_Resistor pull_resistor_1 (.node(pull_resistor_1_node));
  Pull_Resistor pull_resistor_2 (.node(pull_resistor_2_node));
  Pull_Resistor pull_resistor_3 (.node(pull_resistor_3_node));
endmodule

module Zero_Flag (
  input  [7:0] in_1,
  output ZERO
);

  wire and_1_out, and_3_out, nor_1_out, nor_2_out, nor_3_out, nor_4_out;

  nor nor_1 (nor_1_out, in_1[0], in_1[1]);
  nor nor_2 (nor_2_out, in_1[2], in_1[3]);
  nor nor_3 (nor_3_out, in_1[4], in_1[5]);
  nor nor_4 (nor_4_out, in_1[6], in_1[7]);
  and and_1 (and_1_out, nor_1_out, nor_2_out);
  and and_2 (ZERO, and_1_out, and_3_out);
  and and_3 (and_3_out, nor_3_out, nor_4_out);
endmodule

module FLAGS (
  input  CARRY,
  input  ZERO,
  input  STORE,
  input  CLOCK,
  input  RESET,
  output CARRY_OUT,
  output ZERO_OUT
);

  Register #(.width(1)) register_1 (.D(CARRY), .en(STORE), .clk(CLOCK), .Q(CARRY_OUT), .clr(RESET));
  Register #(.width(1)) register_2 (.D(ZERO), .en(STORE), .clk(CLOCK), .Q(ZERO_OUT), .clr(RESET));
  LED led_1 (.in(CARRY_OUT));
  Pull_Resistor pull_resistor_1 (.node(CARRY_OUT));
  LED led_2 (.in(ZERO_OUT));
  Pull_Resistor pull_resistor_2 (.node(ZERO_OUT));
endmodule
