// Logisim project 8_bit_computer.circ as structural Verilog: 29 circuits, main circuit SR_Latch
module main (
  input  PM,
  input  Memory_Adress_register_IN,
  input  Instruction_Register_OUT,
  input  Instruction_Register_IN,
  input  RAM_OUT,
  input  RAM_IN,
  input  Program_Counter_OUT,
  input  Count_Enable,
  input  JUMP_Program_Counter_IN,
  input  A_register_IN,
  input  A_register_OUT,
  input  B_register_IN,
  input  B_register_OUT,
  input  Sum_OUT,
  input  Subtract,
  input  Carry_Bit,
  input  Output_Register_IN
);

  wire A_o1, A_o2, A_o3, A_o4, A_o5, A_o6, A_o7, A_o8, AI, and_1_out, and_2_out, AO, B_o1, B_o2, B_o3, B_o4,
       B_o5, B_o6, B_o7, B_o8, bcd_to_7_segment_decoder_3_p1, BI, binary_to_bcd_converter_1_p2,
       binary_to_bcd_converter_1_p4, BO, clock_1_out, clock_2_out, clock_3_out, clock_4_out, clock_5_out,
       clock_6_out, clock_7_out, clock_8_out, dipswitch_1_sw1, dipswitch_1_sw2, dipswitch_1_sw3,
       dipswitch_1_sw4, dipswitch_1_sw5, dipswitch_1_sw6, dipswitch_1_sw7, dipswitch_1_sw8, dipswitch_2_sw1,
       dipswitch_2_sw2, dipswitch_2_sw3, dipswitch_2_sw4, display_1_out_11, display_1_out_12,
       display_1_out_13, display_1_out_14, display_1_out_15, display_1_out_16, display_1_out_17,
       display_1_out_18, display_1_out_19, display_1_out_20, display_1_out_21, display_1_out_22,
       display_1_out_23, display_1_out_24, display_1_out_25, display_1_out_26, display_1_out_27,
       display_1_out_28, display_1_out_29, display_1_out_30, display_1_out_31, display_1_out_32,
       display_1_out_33, display_1_out_34, display_1_out_35, display_1_out_36, display_1_out_37,
       display_1_out_38, IR_o5, IR_o6, IR_o7, IR_o8, J, MAR_a0, MAR_a1, MAR_a2, MAR_a3, MemoryEN, nand_1_out,
       not_1_out, not_2_out, not_3_out, or_1_out, output_register_1_o1, output_register_1_o2,
       output_register_1_o3, output_register_1_o4, output_register_1_o5, output_register_1_o6,
       output_register_1_o7, output_register_1_o8, program_counter_1_o1, program_counter_1_o2,
       program_counter_1_o3, program_counter_1_o4;
  wire [3:0] multiplexer_2line_to_1line_4bit_1_o0;
  wire [7:0] IR_o1, multiplexer_2line_to_1line_8bit_1_o0;

  LED led_1 (.in(MemoryEN));
  Button button_1 (.out(MemoryEN));
  LedBar ledbar_1 (
    .led0(dipswitch_1_sw1), .led1(dipswitch_1_sw2), .led2(dipswitch_1_sw3), .led3(dipswitch_1_sw4),
    .led4(dipswitch_1_sw5), .led5(dipswitch_1_sw6), .led6(dipswitch_1_sw7), .led7(dipswitch_1_sw8));
  DipSwitch dipswitch_1 (
    .sw1(dipswitch_1_sw1), .sw2(dipswitch_1_sw2), .sw3(dipswitch_1_sw3), .sw4(dipswitch_1_sw4),
    .sw5(dipswitch_1_sw5), .sw6(dipswitch_1_sw6), .sw7(dipswitch_1_sw7), .sw8(dipswitch_1_sw8));
  LedBar #(.matrixcols(4)) ledbar_2 (
    .led0(dipswitch_2_sw1), .led1(dipswitch_2_sw2), .led2(dipswitch_2_sw3), .led3(dipswitch_2_sw4));
  DipSwitch #(.number(4)) dipswitch_2 (
    .sw1(dipswitch_2_sw1), .sw2(dipswitch_2_sw2), .sw3(dipswitch_2_sw3), .sw4(dipswitch_2_sw4));
  LED led_2 (.in(PM));
  Clock clock_1 (.out(clock_1_out));
  Clock clock_2 (.out(clock_2_out));
  Instruction_Register IR (
    .Enable(Instruction_Register_OUT), .Clock(clock_1_out), .Load(Instruction_Register_IN), .D1(IR_o1[0]),
    .D2(IR_o1[1]), .D3(IR_o1[2]), .D4(IR_o1[3]), .D5(IR_o1[4]), .D6(IR_o1[5]), .D7(IR_o1[6]), .D8(IR_o1[7]),
    .O1(IR_o1[0]), .O2(IR_o1[1]), .O3(IR_o1[2]), .O4(IR_o1[3]), .O5(IR_o5), .O6(IR_o6), .O7(IR_o7), .O8(IR_o8));
  Multiplexer_2line_to_1line_8Bit multiplexer_2line_to_1line_8bit_1 (
    .S(PM), .A0(dipswitch_1_sw8), .A1(dipswitch_1_sw7), .A2(dipswitch_1_sw6), .A3(dipswitch_1_sw5),
    .A4(dipswitch_1_sw4), .A5(dipswitch_1_sw3), .A6(dipswitch_1_sw2), .A7(dipswitch_1_sw1), .B0(IR_o1[0]),
    .B1(IR_o1[1]), .B2(IR_o1[2]), .B3(IR_o1[3]), .B4(IR_o1[4]), .B5(IR_o1[5]), .B6(IR_o1[6]), .B7(IR_o1[7]),
    .O0(multiplexer_2line_to_1line_8bit_1_o0[0]), .O1(multiplexer_2line_to_1line_8bit_1_o0[1]),
    .O2(multiplexer_2line_to_1line_8bit_1_o0[2]), .O3(multiplexer_2line_to_1line_8bit_1_o0[3]),
    .O4(multiplexer_2line_to_1line_8bit_1_o0[4]), .O5(multiplexer_2line_to_1line_8bit_1_o0[5]),
    .O6(multiplexer_2line_to_1line_8bit_1_o0[6]), .O7(multiplexer_2line_to_1line_8bit_1_o0[7]));
  Multiplexer_2line_to_1line_4Bit multiplexer_2line_to_1line_4bit_1 (
    .S(PM), .A0(dipswitch_2_sw4), .A1(dipswitch_2_sw3), .A2(dipswitch_2_sw2), .A3(dipswitch_2_sw1),
    .B0(MAR_a0), .B1(MAR_a1), .B2(MAR_a2), .B3(MAR_a3), .O0(multiplexer_2line_to_1line_4bit_1_o0[0]),
    .O1(multiplexer_2line_to_1line_4bit_1_o0[1]), .O2(multiplexer_2line_to_1line_4bit_1_o0[2]),
    .O3(multiplexer_2line_to_1line_4bit_1_o0[3]));
  Memory_Address_Register MAR (
    .Load(Memory_Adress_register_IN), .Clock(clock_2_out), .D1(IR_o1[0]), .D2(IR_o1[1]), .D3(IR_o1[2]),
    .D4(IR_o1[3]), .A0(MAR_a0), .A1(MAR_a1), .A2(MAR_a2), .A3(MAR_a3));
  LED led_3 (.in(IR_o1[0]));
  LED led_4 (.in(IR_o1[1]));
  not not_1 (not_1_out, PM);
  Clock clock_3 (.out(clock_3_out));
  LED led_5 (.in(IR_o5));
  LED led_6 (.in(IR_o6));
  LED led_7 (.in(IR_o1[2]));
  LED led_8 (.in(IR_o1[3]));
  and and_1 (and_1_out, PM, not_2_out);
  not not_2 (not_2_out, MemoryEN);
  and and_2 (and_2_out, not_1_out, nand_1_out);
  nand nand_1 (nand_1_out, clock_3_out, RAM_IN);
  LED led_9 (.in(IR_o7));
  LED led_10 (.in(IR_o8));
  Clock clock_4 (.out(clock_4_out));
  or or_1 (or_1_out, and_1_out, and_2_out);
  RAM #(.addrWidth(4), .\type ("nonvolatile")) ram_1 (
    .addr(multiplexer_2line_to_1line_4bit_1_o0), .we(not_3_out), .oe(RAM_OUT), .clk(clock_4_out),
    .din(multiplexer_2line_to_1line_8bit_1_o0), .dout(IR_o1));
  not not_3 (not_3_out, or_1_out);
  LED led_11 (.in(IR_o1[7]));
  LED led_12 (.in(IR_o1[6]));
  LED led_13 (.in(IR_o1[5]));
  LED led_14 (.in(IR_o1[4]));
  LED led_15 (.in(IR_o1[3]));
  LED led_16 (.in(IR_o1[2]));
  LED led_17 (.in(IR_o1[1]));
  LED led_18 (.in(IR_o1[0]));
  Clock clock_5 (.out(clock_5_out));
  Clock clock_6 (.out(clock_6_out));
  Clock clock_7 (.out(clock_7_out));
  Clock clock_8 (.out(clock_8_out));
  // BCD_to_7_Segment_decoder bcd_to_7_segment_decoder_1: pin names not known
  // BCD_to_7_Segment_decoder bcd_to_7_segment_decoder_2: pin names not known
  // Binary_to_BCD_converter #(.binvalue(8)) binary_to_bcd_converter_1: pin names not known; wires that end beside it: IR_o1, binary_to_bcd_converter_1_p2, binary_to_bcd_converter_1_p2, binary_to_bcd_converter_1_p4, binary_to_bcd_converter_1_p4
  not not_4 (J, JUMP_Program_Counter_IN);
  not not_5 (AI, A_register_IN);
  not not_6 (AO, A_register_OUT);
  not not_7 (BI, B_register_IN);
  not not_8 (BO, B_register_OUT);
  // BCD_to_7_Segment_decoder bcd_to_7_segment_decoder_3: pin names not known; wires that end beside it: bcd_to_7_segment_decoder_3_p1, bcd_to_7_segment_decoder_3_p1
  LED led_19 (.in(program_counter_1_o4));
  LED led_20 (.in(program_counter_1_o3));
  LED led_21 (.in(program_counter_1_o2));
  Program_Counter program_counter_1 (
    .Count_Enable_CE(Count_Enable), .Clock(clock_5_out), .A(IR_o1[0]), .B(IR_o1[1]), .C(IR_o1[2]),
    .D(IR_o1[3]), .Jump_inverted(J), .O1(program_counter_1_o1), .O2(program_counter_1_o2),
    .O3(program_counter_1_o3), .O4(program_counter_1_o4));
  Eight_Bit_Register_Tri_State_logic A (
    .Clock(clock_6_out), .Load(AI), .D1(IR_o1[0]), .D2(IR_o1[1]), .D3(IR_o1[2]), .D4(IR_o1[3]),
    .D5(IR_o1[4]), .D6(IR_o1[5]), .D7(IR_o1[6]), .D8(IR_o1[7]), .Enable(AO), .o1(A_o1), .o2(A_o2), .o3(A_o3),
    .o4(A_o4), .o5(A_o5), .o6(A_o6), .o7(A_o7), .o8(A_o8));
  Eight_Bit_Register_Tri_State_logic B (
    .Clock(clock_7_out), .Load(BI), .D1(IR_o1[0]), .D2(IR_o1[1]), .D3(IR_o1[2]), .D4(IR_o1[3]),
    .D5(IR_o1[4]), .D6(IR_o1[5]), .D7(IR_o1[6]), .D8(IR_o1[7]), .Enable(BO), .o1(B_o1), .o2(B_o2), .o3(B_o3),
    .o4(B_o4), .o5(B_o5), .o6(B_o6), .o7(B_o7), .o8(B_o8));
  Output_Register output_register_1 (
    .Clock(clock_8_out), .Control(Output_Register_IN), .D1(IR_o1[0]), .D2(IR_o1[1]), .D3(IR_o1[2]),
    .D4(IR_o1[3]), .D5(IR_o1[4]), .D6(IR_o1[5]), .D7(IR_o1[6]), .D8(IR_o1[7]), .O8(output_register_1_o8),
    .O7(output_register_1_o7), .O6(output_register_1_o6), .O5(output_register_1_o5),
    .O4(output_register_1_o4), .O3(output_register_1_o3), .O2(output_register_1_o2), .O1(output_register_1_o1));
  LED led_22 (.in(program_counter_1_o1));
  assign IR_o1[0] = Program_Counter_OUT ? program_counter_1_o1 : 1'bz;  // Controlled_Buffer controlled_buffer_1
  assign IR_o1[1] = Program_Counter_OUT ? program_counter_1_o2 : 1'bz;  // Controlled_Buffer controlled_buffer_2
  assign IR_o1[2] = Program_Counter_OUT ? program_counter_1_o3 : 1'bz;  // Controlled_Buffer controlled_buffer_3
  assign IR_o1[3] = Program_Counter_OUT ? program_counter_1_o4 : 1'bz;  // Controlled_Buffer controlled_buffer_4
  Display display_1 (
    .D8(output_register_1_o8), .D7(output_register_1_o7), .D6(output_register_1_o6),
    .D5(output_register_1_o5), .D4(output_register_1_o4), .D3(output_register_1_o3),
    .D2(output_register_1_o2), .D1(output_register_1_o1), .out_11(display_1_out_11),
    .out_12(display_1_out_12), .out_13(display_1_out_13), .out_14(display_1_out_14),
    .out_15(display_1_out_15), .out_16(display_1_out_16), .out_17(display_1_out_17),
    .out_18(display_1_out_18), .out_19(display_1_out_19), .out_20(display_1_out_20),
    .out_21(display_1_out_21), .out_22(display_1_out_22), .out_23(display_1_out_23),
    .out_24(display_1_out_24), .out_25(display_1_out_25), .out_26(display_1_out_26),
    .out_27(display_1_out_27), .out_28(display_1_out_28), .out_29(display_1_out_29),
    .out_30(display_1_out_30), .out_31(display_1_out_31), .out_32(display_1_out_32),
    .out_33(display_1_out_33), .out_34(display_1_out_34), .out_35(display_1_out_35),
    .out_36(display_1_out_36), .out_37(display_1_out_37), .out_38(display_1_out_38));  // open: RB, TwoS_Complement
  ALU alu_1 (
    .A1(A_o1), .A2(A_o2), .A3(A_o3), .A4(A_o4), .A5(A_o5), .A6(A_o6), .A7(A_o7), .A8(A_o8),
    .Carry_Bit(Carry_Bit), .SUB(Subtract), .B1(B_o1), .B2(B_o2), .B3(B_o3), .B4(B_o4), .B5(B_o5), .B6(B_o6),
    .B7(B_o7), .B8(B_o8), .E0(Sum_OUT), .O1(IR_o1[0]), .O2(IR_o1[1]), .O3(IR_o1[2]), .O4(IR_o1[3]),
    .O5(IR_o1[4]), .O6(IR_o1[5]), .O7(IR_o1[6]), .O8(IR_o1[7]));
  _7_Segment_Display u_7_segment_display_1 (
    .g(display_1_out_17), .f(display_1_out_16), .a(display_1_out_11), .b(display_1_out_12),
    .e(display_1_out_15), .d(display_1_out_14), .c(display_1_out_13));  // open: dp
  _7_Segment_Display u_7_segment_display_2 (
    .g(display_1_out_24), .f(display_1_out_23), .a(display_1_out_18), .b(display_1_out_19),
    .e(display_1_out_22), .d(display_1_out_21), .c(display_1_out_20));  // open: dp
  _7_Segment_Display u_7_segment_display_3 (
    .g(display_1_out_31), .f(display_1_out_30), .a(display_1_out_25), .b(display_1_out_26),
    .e(display_1_out_29), .d(display_1_out_28), .c(display_1_out_27));  // open: dp
  _7_Segment_Display u_7_segment_display_4 (
    .g(display_1_out_38), .f(display_1_out_37), .a(display_1_out_32), .b(display_1_out_33),
    .e(display_1_out_36), .d(display_1_out_35), .c(display_1_out_34));  // open: dp

  // Other names for the same wires on the sheet: CE = Count_Enable; CO = Program_Counter_OUT; CY = Carry_Bit;
  //   E0 = Sum_OUT; II = Instruction_Register_IN; IO = Instruction_Register_OUT; MI = Memory_Adress_register_IN;
  //   OI = Output_Register_IN; RI = RAM_IN; RO = RAM_OUT; SU = Subtract

  // Notes on the sheet:
  //   Memory IN
  //   POWER => PROGRAMMING MODE
  //   WR
endmodule

module SR_Latch (
  input  Reset,
  input  Set,
  output Q,
  output QC
);

  nor nor_1 (Q, Reset, QC);
  nor nor_2 (QC, Q, Set);
endmodule

module D_Latch (
  input  Store,
  input  Data,
  output Q,
  output QC
);

  wire and_1_out, and_2_out, not_1_out;

  not not_1 (not_1_out, Data);
  and and_1 (and_1_out, not_1_out, Store);
  and and_2 (and_2_out, Store, Data);
  nor nor_1 (Q, and_1_out, QC);
  nor nor_2 (QC, Q, and_2_out);
endmodule

module One_Bit_Register (
  input  Load,
  input  Data,
  input  Clock,
  output O
);

  wire and_1_out, and_2_out, not_1_out, or_1_out;

  not not_1 (not_1_out, Load);
  and and_1 (and_1_out, O, not_1_out);
  and and_2 (and_2_out, Load, Data);
  or or_1 (or_1_out, and_1_out, and_2_out);
  D_Flip_Flop d_ff_1 (.D(or_1_out), .clk(Clock), .Q(O));  // open: Qn, preset, reset
endmodule

module Eight_Bit_Register (
  input  Clock,
  input  Load,
  input  D1,
  input  D2,
  input  D3,
  input  D4,
  input  D5,
  input  D6,
  input  D7,
  input  D8,
  output o1,
  output o2,
  output o3,
  output o4,
  output o5,
  output o6,
  output o7,
  output o8
);

  One_Bit_Register one_bit_register_1 (.Load(Load), .Data(D1), .Clock(Clock), .O(o1));
  One_Bit_Register one_bit_register_2 (.Load(Load), .Data(D2), .Clock(Clock), .O(o2));
  One_Bit_Register one_bit_register_3 (.Load(Load), .Data(D3), .Clock(Clock), .O(o3));
  One_Bit_Register one_bit_register_4 (.Load(Load), .Data(D4), .Clock(Clock), .O(o4));
  One_Bit_Register one_bit_register_5 (.Load(Load), .Data(D5), .Clock(Clock), .O(o5));
  One_Bit_Register one_bit_register_6 (.Load(Load), .Data(D6), .Clock(Clock), .O(o6));
  One_Bit_Register one_bit_register_7 (.Load(Load), .Data(D7), .Clock(Clock), .O(o7));
  One_Bit_Register one_bit_register_8 (.Load(Load), .Data(D8), .Clock(Clock), .O(o8));
endmodule

module Tri_state_Buffer (
  input  i1,
  input  i2,
  input  i3,
  input  i4,
  input  i5,
  input  l6,
  input  i7,
  input  i8,
  input  Enable,
  output o1,
  output o2,
  output o3,
  output o4,
  output o5,
  output o6,
  output o7,
  output o8
);

  assign o1 = Enable ? i1 : 1'bz;  // Controlled_Buffer controlled_buffer_1
  assign o2 = Enable ? i2 : 1'bz;  // Controlled_Buffer controlled_buffer_2
  assign o3 = Enable ? i3 : 1'bz;  // Controlled_Buffer controlled_buffer_3
  assign o4 = Enable ? i4 : 1'bz;  // Controlled_Buffer controlled_buffer_4
  assign o5 = Enable ? i5 : 1'bz;  // Controlled_Buffer controlled_buffer_5
  assign o6 = Enable ? l6 : 1'bz;  // Controlled_Buffer controlled_buffer_6
  assign o7 = Enable ? i7 : 1'bz;  // Controlled_Buffer controlled_buffer_7
  assign o8 = Enable ? i8 : 1'bz;  // Controlled_Buffer controlled_buffer_8
endmodule

module Eight_Bit_Register_Tri_State_logic (
  input  Clock,
  input  Load,
  input  D1,
  input  D2,
  input  D3,
  input  D4,
  input  D5,
  input  D6,
  input  D7,
  input  D8,
  input  Enable,
  output o1,
  output o2,
  output o3,
  output o4,
  output o5,
  output o6,
  output o7,
  output o8
);

  wire eight_bit_register_1_o1, eight_bit_register_1_o2, eight_bit_register_1_o3, eight_bit_register_1_o4,
       eight_bit_register_1_o5, eight_bit_register_1_o6, eight_bit_register_1_o7, eight_bit_register_1_o8,
       not_1_out, not_2_out;

  not not_1 (not_1_out, Load);
  not not_2 (not_2_out, Enable);
  Eight_Bit_Register eight_bit_register_1 (
    .Clock(Clock), .Load(not_1_out), .D1(D1), .D2(D2), .D3(D3), .D4(D4), .D5(D5), .D6(D6), .D7(D7), .D8(D8),
    .o1(eight_bit_register_1_o1), .o2(eight_bit_register_1_o2), .o3(eight_bit_register_1_o3),
    .o4(eight_bit_register_1_o4), .o5(eight_bit_register_1_o5), .o6(eight_bit_register_1_o6),
    .o7(eight_bit_register_1_o7), .o8(eight_bit_register_1_o8));
  Tri_state_Buffer tri_state_buffer_1 (
    .i1(eight_bit_register_1_o1), .i2(eight_bit_register_1_o2), .i3(eight_bit_register_1_o3),
    .i4(eight_bit_register_1_o4), .i5(eight_bit_register_1_o5), .l6(eight_bit_register_1_o6),
    .i7(eight_bit_register_1_o7), .i8(eight_bit_register_1_o8), .Enable(not_2_out), .o1(o1), .o2(o2),
    .o3(o3), .o4(o4), .o5(o5), .o6(o6), .o7(o7), .o8(o8));
endmodule

module Instruction_Register (
  input  Enable,
  input  Clock,
  input  Load,
  input  D1,
  input  D2,
  input  D3,
  input  D4,
  input  D5,
  input  D6,
  input  D7,
  input  D8,
  output O1,
  output O2,
  output O3,
  output O4,
  output O5,
  output O6,
  output O7,
  output O8
);

  wire eight_bit_register_1_o1, eight_bit_register_1_o2, eight_bit_register_1_o3, eight_bit_register_1_o4;

  Eight_Bit_Register eight_bit_register_1 (
    .Clock(Clock), .Load(Load), .D1(D1), .D2(D2), .D3(D3), .D4(D4), .D5(D5), .D6(D6), .D7(D7), .D8(D8),
    .o1(eight_bit_register_1_o1), .o2(eight_bit_register_1_o2), .o3(eight_bit_register_1_o3),
    .o4(eight_bit_register_1_o4), .o5(O5), .o6(O6), .o7(O7), .o8(O8));
  assign O1 = Enable ? eight_bit_register_1_o1 : 1'bz;  // Controlled_Buffer controlled_buffer_1
  assign O2 = Enable ? eight_bit_register_1_o2 : 1'bz;  // Controlled_Buffer controlled_buffer_2
  assign O3 = Enable ? eight_bit_register_1_o3 : 1'bz;  // Controlled_Buffer controlled_buffer_3
  assign O4 = Enable ? eight_bit_register_1_o4 : 1'bz;  // Controlled_Buffer controlled_buffer_4
endmodule

module Full_Adder (
  input  A,
  input  B,
  input  Cin,
  output S,
  output Cout
);

  wire and_1_out, and_2_out, xor_1_out;

  xor xor_1 (xor_1_out, A, B);
  and and_1 (and_1_out, A, B);
  xor xor_2 (S, xor_1_out, Cin);
  and and_2 (and_2_out, Cin, xor_1_out);
  or or_1 (Cout, and_2_out, and_1_out);
endmodule

module Eight_Bit_Adder (
  input  A1,
  input  A2,
  input  A3,
  input  A4,
  input  A5,
  input  A6,
  input  A7,
  input  A8,
  input  Cin,
  input  B1,
  input  B2,
  input  B3,
  input  B4,
  input  B5,
  input  B6,
  input  B7,
  input  B8,
  output S1,
  output S2,
  output S3,
  output S4,
  output S5,
  output S6,
  output S7,
  output S8,
  output Cout
);

  wire full_adder_1_cout, full_adder_2_cout, full_adder_3_cout, full_adder_4_cout, full_adder_5_cout,
       full_adder_6_cout, full_adder_7_cout;

  Full_Adder full_adder_1 (.A(A1), .B(B1), .Cin(Cin), .S(S1), .Cout(full_adder_1_cout));
  Full_Adder full_adder_2 (.A(A2), .B(B2), .Cin(full_adder_1_cout), .S(S2), .Cout(full_adder_2_cout));
  Full_Adder full_adder_3 (.A(A3), .B(B3), .Cin(full_adder_2_cout), .S(S3), .Cout(full_adder_3_cout));
  Full_Adder full_adder_4 (.A(A4), .B(B4), .Cin(full_adder_3_cout), .S(S4), .Cout(full_adder_4_cout));
  Full_Adder full_adder_5 (.A(A5), .B(B5), .Cin(full_adder_4_cout), .S(S5), .Cout(full_adder_5_cout));
  Full_Adder full_adder_6 (.A(A6), .B(B6), .Cin(full_adder_5_cout), .S(S6), .Cout(full_adder_6_cout));
  Full_Adder full_adder_7 (.A(A7), .B(B7), .Cin(full_adder_6_cout), .S(S7), .Cout(full_adder_7_cout));
  Full_Adder full_adder_8 (.A(A8), .B(B8), .Cin(full_adder_7_cout), .S(S8), .Cout(Cout));
endmodule

module ALU (
  input  A1,
  input  A2,
  input  A3,
  input  A4,
  input  A5,
  input  A6,
  input  A7,
  input  A8,
  input  Carry_Bit,
  input  SUB,
  input  B1,
  input  B2,
  input  B3,
  input  B4,
  input  B5,
  input  B6,
  input  B7,
  input  B8,
  input  E0,
  output O1,
  output O2,
  output O3,
  output O4,
  output O5,
  output O6,
  output O7,
  output O8
);

  wire eight_bit_adder_1_s1, eight_bit_adder_1_s2, eight_bit_adder_1_s3, eight_bit_adder_1_s4,
       eight_bit_adder_1_s5, eight_bit_adder_1_s6, eight_bit_adder_1_s7, eight_bit_adder_1_s8, xor_1_out,
       xor_2_out, xor_3_out, xor_4_out, xor_5_out, xor_6_out, xor_7_out, xor_8_out;

  xor xor_1 (xor_1_out, B1, Carry_Bit);
  xor xor_2 (xor_2_out, B2, Carry_Bit);
  xor xor_3 (xor_3_out, B3, Carry_Bit);
  xor xor_4 (xor_4_out, B4, Carry_Bit);
  xor xor_5 (xor_5_out, B5, Carry_Bit);
  xor xor_6 (xor_6_out, B6, Carry_Bit);
  xor xor_7 (xor_7_out, B7, Carry_Bit);
  xor xor_8 (xor_8_out, B8, Carry_Bit);
  Eight_Bit_Adder eight_bit_adder_1 (
    .A1(A1), .A2(A2), .A3(A3), .A4(A4), .A5(A5), .A6(A6), .A7(A7), .A8(A8), .Cin(Carry_Bit), .B1(xor_1_out),
    .B2(xor_2_out), .B3(xor_3_out), .B4(xor_4_out), .B5(xor_5_out), .B6(xor_6_out), .B7(xor_7_out),
    .B8(xor_8_out), .S1(eight_bit_adder_1_s1), .S2(eight_bit_adder_1_s2), .S3(eight_bit_adder_1_s3),
    .S4(eight_bit_adder_1_s4), .S5(eight_bit_adder_1_s5), .S6(eight_bit_adder_1_s6),
    .S7(eight_bit_adder_1_s7), .S8(eight_bit_adder_1_s8));  // open: Cout
  Tri_state_Buffer tri_state_buffer_1 (
    .i1(eight_bit_adder_1_s1), .i2(eight_bit_adder_1_s2), .i3(eight_bit_adder_1_s3),
    .i4(eight_bit_adder_1_s4), .i5(eight_bit_adder_1_s5), .l6(eight_bit_adder_1_s6),
    .i7(eight_bit_adder_1_s7), .i8(eight_bit_adder_1_s8), .Enable(E0), .o1(O1), .o2(O2), .o3(O3), .o4(O4),
    .o5(O5), .o6(O6), .o7(O7), .o8(O8));

  assign SUB = Carry_Bit;
endmodule

module Asynchronous_One_Bit_Register (
  input  I,
  input  WR,
  input  EN,
  output O
);

  wire d_latch_1_q;

  assign O = EN ? d_latch_1_q : 1'bz;  // Controlled_Buffer controlled_buffer_1
  D_Latch d_latch_1 (.Store(WR), .Data(I), .Q(d_latch_1_q));  // open: QC
endmodule

module Decoder_4_to_16 (
  input  S,
  input  A0,
  input  A1,
  input  A2,
  input  A3,
  output X0,
  output X1,
  output X2,
  output X3,
  output X4,
  output X5,
  output X6,
  output X7,
  output X8,
  output X9,
  output X10,
  output X11,
  output X12,
  output X13,
  output X14,
  output X15
);

  wire not_1_out, not_2_out, not_3_out, not_4_out;

  not not_1 (not_1_out, A0);
  not not_2 (not_2_out, A1);
  not not_3 (not_3_out, A2);
  not not_4 (not_4_out, A3);
  and and_1 (X0, S, not_1_out, not_2_out, not_3_out, not_4_out);
  and and_2 (X1, S, A0, not_2_out, not_3_out, not_4_out);
  and and_3 (X2, S, not_1_out, A1, not_3_out, not_4_out);
  and and_4 (X3, S, A0, A1, not_3_out, not_4_out);
  and and_5 (X4, S, not_1_out, not_2_out, A2, not_4_out);
  and and_6 (X5, S, A0, not_2_out, A2, not_4_out);
  and and_7 (X6, S, not_1_out, A1, A2, not_4_out);
  and and_8 (X7, S, A0, A1, A2, not_4_out);
  and and_9 (X8, S, not_1_out, not_2_out, not_3_out, A3);
  and and_10 (X9, S, A0, not_2_out, not_3_out, A3);
  and and_11 (X10, S, not_1_out, A1, not_3_out, A3);
  and and_12 (X11, S, A0, A1, not_3_out, A3);
  and and_13 (X12, S, not_1_out, not_2_out, A2, A3);
  and and_14 (X13, S, A0, not_2_out, A2, A3);
  and and_15 (X14, S, not_1_out, A1, A2, A3);
  and and_16 (X15, S, A0, A1, A2, A3);
endmodule

module Static_RAM_16_Word_8_Bit_array (
  input  D1,
  input  D2,
  input  D3,
  input  D4,
  input  D5,
  input  D6,
  input  D7,
  input  D8,
  input  WR0,
  input  EN0,
  input  WR1,
  input  EN1,
  input  WR2,
  input  EN2,
  input  WR3,
  input  EN3,
  input  WR4,
  input  EN4,
  input  WR5,
  input  EN5,
  input  WR6,
  input  EN6,
  input  WR7,
  input  EN7,
  input  WR8,
  input  EN8,
  input  WR9,
  input  EN9,
  input  WR10,
  input  EN10,
  input  WR11,
  input  EN11,
  input  WR12,
  input  EN12,
  input  WR13,
  input  EN13,
  input  WR14,
  input  EN14,
  input  WR15,
  input  EN15,
  output O1,
  output O2,
  output O3,
  output O4,
  output O5,
  output O6,
  output O7,
  output O8
);

  Asynchronous_One_Bit_Register asynchronous_one_bit_register_1 (.I(D1), .WR(WR0), .EN(EN0), .O(O1));
  Asynchronous_One_Bit_Register asynchronous_one_bit_register_2 (.I(D1), .WR(WR1), .EN(EN1), .O(O1));
  Asynchronous_One_Bit_Register asynchronous_one_bit_register_3 (.I(D1), .WR(WR2), .EN(EN2), .O(O1));
  Asynchronous_One_Bit_Register asynchronous_one_bit_register_4 (.I(D1), .WR(WR3), .EN(EN3), .O(O1));
  Asynchronous_One_Bit_Register asynchronous_one_bit_register_5 (.I(D1), .WR(WR4), .EN(EN4), .O(O1));
  Asynchronous_One_Bit_Register asynchronous_one_bit_register_6 (.I(D1), .WR(WR5), .EN(EN5), .O(O1));
  Asynchronous_One_Bit_Register asynchronous_one_bit_register_7 (.I(D1), .WR(WR6), .EN(EN6), .O(O1));
  Asynchronous_One_Bit_Register asynchronous_one_bit_register_8 (.I(D1), .WR(WR7), .EN(EN7), .O(O1));
  Asynchronous_One_Bit_Register asynchronous_one_bit_register_9 (.I(D1), .WR(WR8), .EN(EN8), .O(O1));
  Asynchronous_One_Bit_Register asynchronous_one_bit_register_10 (.I(D1), .WR(WR9), .EN(EN9), .O(O1));
  Asynchronous_One_Bit_Register asynchronous_one_bit_register_11 (.I(D1), .WR(WR10), .EN(EN10), .O(O1));
  Asynchronous_One_Bit_Register asynchronous_one_bit_register_12 (.I(D1), .WR(WR11), .EN(EN11), .O(O1));
  Asynchronous_One_Bit_Register asynchronous_one_bit_register_13 (.I(D1), .WR(WR12), .EN(EN12), .O(O1));
  Asynchronous_One_Bit_Register asynchronous_one_bit_register_14 (.I(D1), .WR(WR13), .EN(EN13), .O(O1));
  Asynchronous_One_Bit_Register asynchronous_one_bit_register_15 (.I(D1), .WR(WR14), .EN(EN14), .O(O1));
  Asynchronous_One_Bit_Register asynchronous_one_bit_register_16 (.I(D1), .WR(WR15), .EN(EN15), .O(O1));
  Asynchronous_One_Bit_Register asynchronous_one_bit_register_17 (.I(D2), .WR(WR0), .EN(EN0), .O(O2));
  Asynchronous_One_Bit_Register asynchronous_one_bit_register_18 (.I(D2), .WR(WR1), .EN(EN1), .O(O2));
  Asynchronous_One_Bit_Register asynchronous_one_bit_register_19 (.I(D2), .WR(WR2), .EN(EN2), .O(O2));
  Asynchronous_One_Bit_Register asynchronous_one_bit_register_20 (.I(D2), .WR(WR3), .EN(EN3), .O(O2));
  Asynchronous_One_Bit_Register asynchronous_one_bit_register_21 (.I(D2), .WR(WR4), .EN(EN4), .O(O2));
  Asynchronous_One_Bit_Register asynchronous_one_bit_register_22 (.I(D2), .WR(WR5), .EN(EN5), .O(O2));
  Asynchronous_One_Bit_Register asynchronous_one_bit_register_23 (.I(D2), .WR(WR6), .EN(EN6), .O(O2));
  Asynchronous_One_Bit_Register asynchronous_one_bit_register_24 (.I(D2), .WR(WR7), .EN(EN7), .O(O2));
  Asynchronous_One_Bit_Register asynchronous_one_bit_register_25 (.I(D2), .WR(WR8), .EN(EN8), .O(O2));
  Asynchronous_One_Bit_Register asynchronous_one_bit_register_26 (.I(D2), .WR(WR9), .EN(EN9), .O(O2));
  Asynchronous_One_Bit_Register asynchronous_one_bit_register_27 (.I(D2), .WR(WR10), .EN(EN10), .O(O2));
  Asynchronous_One_Bit_Register asynchronous_one_bit_register_28 (.I(D2), .WR(WR11), .EN(EN11), .O(O2));
  Asynchronous_One_Bit_Register asynchronous_one_bit_register_29 (.I(D2), .WR(WR12), .EN(EN12), .O(O2));
  Asynchronous_One_Bit_Register asynchronous_one_bit_register_30 (.I(D2), .WR(WR13), .EN(EN13), .O(O2));
  Asynchronous_One_Bit_Register asynchronous_one_bit_register_31 (.I(D2), .WR(WR14), .EN(EN14), .O(O2));
  Asynchronous_One_Bit_Register asynchronous_one_bit_register_32 (.I(D2), .WR(WR15), .EN(EN15), .O(O2));
  Asynchronous_One_Bit_Register asynchronous_one_bit_register_33 (.I(D3), .WR(WR0), .EN(EN0), .O(O3));
  Asynchronous_One_Bit_Register asynchronous_one_bit_register_34 (.I(D3), .WR(WR1), .EN(EN1), .O(O3));
  Asynchronous_One_Bit_Register asynchronous_one_bit_register_35 (.I(D3), .WR(WR2), .EN(EN2), .O(O3));
  Asynchronous_One_Bit_Register asynchronous_one_bit_register_36 (.I(D3), .WR(WR3), .EN(EN3), .O(O3));
  Asynchronous_One_Bit_Register asynchronous_one_bit_register_37 (.I(D3), .WR(WR4), .EN(EN4), .O(O3));
  Asynchronous_One_Bit_Register asynchronous_one_bit_register_38 (.I(D3), .WR(WR5), .EN(EN5), .O(O3));
  Asynchronous_One_Bit_Register asynchronous_one_bit_register_39 (.I(D3), .WR(WR6), .EN(EN6), .O(O3));
  Asynchronous_One_Bit_Register asynchronous_one_bit_register_40 (.I(D3), .WR(WR7), .EN(EN7), .O(O3));
  Asynchronous_One_Bit_Register asynchronous_one_bit_register_41 (.I(D3), .WR(WR8), .EN(EN8), .O(O3));
  Asynchronous_One_Bit_Register asynchronous_one_bit_register_42 (.I(D3), .WR(WR9), .EN(EN9), .O(O3));
  Asynchronous_One_Bit_Register asynchronous_one_bit_register_43 (.I(D3), .WR(WR10), .EN(EN10), .O(O3));
  Asynchronous_One_Bit_Register asynchronous_one_bit_register_44 (.I(D3), .WR(WR11), .EN(EN11), .O(O3));
  Asynchronous_One_Bit_Register asynchronous_one_bit_register_45 (.I(D3), .WR(WR12), .EN(EN12), .O(O3));
  Asynchronous_One_Bit_Register asynchronous_one_bit_register_46 (.I(D3), .WR(WR13), .EN(EN13), .O(O3));
  Asynchronous_One_Bit_Register asynchronous_one_bit_register_47 (.I(D3), .WR(WR14), .EN(EN14), .O(O3));
  Asynchronous_One_Bit_Register asynchronous_one_bit_register_48 (.I(D3), .WR(WR15), .EN(EN15), .O(O3));
  Asynchronous_One_Bit_Register asynchronous_one_bit_register_49 (.I(D4), .WR(WR0), .EN(EN0), .O(O4));
  Asynchronous_One_Bit_Register asynchronous_one_bit_register_50 (.I(D4), .WR(WR1), .EN(EN1), .O(O4));
  Asynchronous_One_Bit_Register asynchronous_one_bit_register_51 (.I(D4), .WR(WR2), .EN(EN2), .O(O4));
  Asynchronous_One_Bit_Register asynchronous_one_bit_register_52 (.I(D4), .WR(WR3), .EN(EN3), .O(O4));
  Asynchronous_One_Bit_Register asynchronous_one_bit_register_53 (.I(D4), .WR(WR4), .EN(EN4), .O(O4));
  Asynchronous_One_Bit_Register asynchronous_one_bit_register_54 (.I(D4), .WR(WR5), .EN(EN5), .O(O4));
  Asynchronous_One_Bit_Register asynchronous_one_bit_register_55 (.I(D4), .WR(WR6), .EN(EN6), .O(O4));
  Asynchronous_One_Bit_Register asynchronous_one_bit_register_56 (.I(D4), .WR(WR7), .EN(EN7), .O(O4));
  Asynchronous_One_Bit_Register asynchronous_one_bit_register_57 (.I(D4), .WR(WR8), .EN(EN8), .O(O4));
  Asynchronous_One_Bit_Register asynchronous_one_bit_register_58 (.I(D4), .WR(WR9), .EN(EN9), .O(O4));
  Asynchronous_One_Bit_Register asynchronous_one_bit_register_59 (.I(D4), .WR(WR10), .EN(EN10), .O(O4));
  Asynchronous_One_Bit_Register asynchronous_one_bit_register_60 (.I(D4), .WR(WR11), .EN(EN11), .O(O4));
  Asynchronous_One_Bit_Register asynchronous_one_bit_register_61 (.I(D4), .WR(WR12), .EN(EN12), .O(O4));
  Asynchronous_One_Bit_Register asynchronous_one_bit_register_62 (.I(D4), .WR(WR13), .EN(EN13), .O(O4));
  Asynchronous_One_Bit_Register asynchronous_one_bit_register_63 (.I(D4), .WR(WR14), .EN(EN14), .O(O4));
  Asynchronous_One_Bit_Register asynchronous_one_bit_register_64 (.I(D4), .WR(WR15), .EN(EN15), .O(O4));
  Asynchronous_One_Bit_Register asynchronous_one_bit_register_65 (.I(D5), .WR(WR0), .EN(EN0), .O(O5));
  Asynchronous_One_Bit_Register asynchronous_one_bit_register_66 (.I(D5), .WR(WR1), .EN(EN1), .O(O5));
  Asynchronous_One_Bit_Register asynchronous_one_bit_register_67 (.I(D5), .WR(WR2), .EN(EN2), .O(O5));
  Asynchronous_One_Bit_Register asynchronous_one_bit_register_68 (.I(D5), .WR(WR3), .EN(EN3), .O(O5));
  Asynchronous_One_Bit_Register asynchronous_one_bit_register_69 (.I(D5), .WR(WR4), .EN(EN4), .O(O5));
  Asynchronous_One_Bit_Register asynchronous_one_bit_register_70 (.I(D5), .WR(WR5), .EN(EN5), .O(O5));
  Asynchronous_One_Bit_Register asynchronous_one_bit_register_71 (.I(D5), .WR(WR6), .EN(EN6), .O(O5));
  Asynchronous_One_Bit_Register asynchronous_one_bit_register_72 (.I(D5), .WR(WR7), .EN(EN7), .O(O5));
  Asynchronous_One_Bit_Register asynchronous_one_bit_register_73 (.I(D5), .WR(WR8), .EN(EN8), .O(O5));
  Asynchronous_One_Bit_Register asynchronous_one_bit_register_74 (.I(D5), .WR(WR9), .EN(EN9), .O(O5));
  Asynchronous_One_Bit_Register asynchronous_one_bit_register_75 (.I(D5), .WR(WR10), .EN(EN10), .O(O5));
  Asynchronous_One_Bit_Register asynchronous_one_bit_register_76 (.I(D5), .WR(WR11), .EN(EN11), .O(O5));
  Asynchronous_One_Bit_Register asynchronous_one_bit_register_77 (.I(D5), .WR(WR12), .EN(EN12), .O(O5));
  Asynchronous_One_Bit_Register asynchronous_one_bit_register_78 (.I(D5), .WR(WR13), .EN(EN13), .O(O5));
  Asynchronous_One_Bit_Register asynchronous_one_bit_register_79 (.I(D5), .WR(WR14), .EN(EN14), .O(O5));
  Asynchronous_One_Bit_Register asynchronous_one_bit_register_80 (.I(D5), .WR(WR15), .EN(EN15), .O(O5));
  Asynchronous_One_Bit_Register asynchronous_one_bit_register_81 (.I(D6), .WR(WR0), .EN(EN0), .O(O6));
  Asynchronous_One_Bit_Register asynchronous_one_bit_register_82 (.I(D6), .WR(WR1), .EN(EN1), .O(O6));
  Asynchronous_One_Bit_Register asynchronous_one_bit_register_83 (.I(D6), .WR(WR2), .EN(EN2), .O(O6));
  Asynchronous_One_Bit_Register asynchronous_one_bit_register_84 (.I(D6), .WR(WR3), .EN(EN3), .O(O6));
  Asynchronous_One_Bit_Register asynchronous_one_bit_register_85 (.I(D6), .WR(WR4), .EN(EN4), .O(O6));
  Asynchronous_One_Bit_Register asynchronous_one_bit_register_86 (.I(D6), .WR(WR5), .EN(EN5), .O(O6));
  Asynchronous_One_Bit_Register asynchronous_one_bit_register_87 (.I(D6), .WR(WR6), .EN(EN6), .O(O6));
  Asynchronous_One_Bit_Register asynchronous_one_bit_register_88 (.I(D6), .WR(WR7), .EN(EN7), .O(O6));
  Asynchronous_One_Bit_Register asynchronous_one_bit_register_89 (.I(D6), .WR(WR8), .EN(EN8), .O(O6));
  Asynchronous_One_Bit_Register asynchronous_one_bit_register_90 (.I(D6), .WR(WR9), .EN(EN9), .O(O6));
  Asynchronous_One_Bit_Register asynchronous_one_bit_register_91 (.I(D6), .WR(WR10), .EN(EN10), .O(O6));
  Asynchronous_One_Bit_Register asynchronous_one_bit_register_92 (.I(D6), .WR(WR11), .EN(EN11), .O(O6));
  Asynchronous_One_Bit_Register asynchronous_one_bit_register_93 (.I(D6), .WR(WR12), .EN(EN12), .O(O6));
  Asynchronous_One_Bit_Register asynchronous_one_bit_register_94 (.I(D6), .WR(WR13), .EN(EN13), .O(O6));
  Asynchronous_One_Bit_Register asynchronous_one_bit_register_95 (.I(D6), .WR(WR14), .EN(EN14), .O(O6));
  Asynchronous_One_Bit_Register asynchronous_one_bit_register_96 (.I(D6), .WR(WR15), .EN(EN15), .O(O6));
  Asynchronous_One_Bit_Register asynchronous_one_bit_register_97 (.I(D7), .WR(WR0), .EN(EN0), .O(O7));
  Asynchronous_One_Bit_Register asynchronous_one_bit_register_98 (.I(D7), .WR(WR1), .EN(EN1), .O(O7));
  Asynchronous_One_Bit_Register asynchronous_one_bit_register_99 (.I(D7), .WR(WR2), .EN(EN2), .O(O7));
  Asynchronous_One_Bit_Register asynchronous_one_bit_register_100 (.I(D7), .WR(WR3), .EN(EN3), .O(O7));
  Asynchronous_One_Bit_Register asynchronous_one_bit_register_101 (.I(D7), .WR(WR4), .EN(EN4), .O(O7));
  Asynchronous_One_Bit_Register asynchronous_one_bit_register_102 (.I(D7), .WR(WR5), .EN(EN5), .O(O7));
  Asynchronous_One_Bit_Register asynchronous_one_bit_register_103 (.I(D7), .WR(WR6), .EN(EN6), .O(O7));
  Asynchronous_One_Bit_Register asynchronous_one_bit_register_104 (.I(D7), .WR(WR7), .EN(EN7), .O(O7));
  Asynchronous_One_Bit_Register asynchronous_one_bit_register_105 (.I(D7), .WR(WR8), .EN(EN8), .O(O7));
  Asynchronous_One_Bit_Register asynchronous_one_bit_register_106 (.I(D7), .WR(WR9), .EN(EN9), .O(O7));
  Asynchronous_One_Bit_Register asynchronous_one_bit_register_107 (.I(D7), .WR(WR10), .EN(EN10), .O(O7));
  Asynchronous_One_Bit_Register asynchronous_one_bit_register_108 (.I(D7), .WR(WR11), .EN(EN11), .O(O7));
  Asynchronous_One_Bit_Register asynchronous_one_bit_register_109 (.I(D7), .WR(WR12), .EN(EN12), .O(O7));
  Asynchronous_One_Bit_Register asynchronous_one_bit_register_110 (.I(D7), .WR(WR13), .EN(EN13), .O(O7));
  Asynchronous_One_Bit_Register asynchronous_one_bit_register_111 (.I(D7), .WR(WR14), .EN(EN14), .O(O7));
  Asynchronous_One_Bit_Register asynchronous_one_bit_register_112 (.I(D7), .WR(WR15), .EN(EN15), .O(O7));
  Asynchronous_One_Bit_Register asynchronous_one_bit_register_113 (.I(D8), .WR(WR0), .EN(EN0), .O(O8));
  Asynchronous_One_Bit_Register asynchronous_one_bit_register_114 (.I(D8), .WR(WR1), .EN(EN1), .O(O8));
  Asynchronous_One_Bit_Register asynchronous_one_bit_register_115 (.I(D8), .WR(WR2), .EN(EN2), .O(O8));
  Asynchronous_One_Bit_Register asynchronous_one_bit_register_116 (.I(D8), .WR(WR3), .EN(EN3), .O(O8));
  Asynchronous_One_Bit_Register asynchronous_one_bit_register_117 (.I(D8), .WR(WR4), .EN(EN4), .O(O8));
  Asynchronous_One_Bit_Register asynchronous_one_bit_register_118 (.I(D8), .WR(WR5), .EN(EN5), .O(O8));
  Asynchronous_One_Bit_Register asynchronous_one_bit_register_119 (.I(D8), .WR(WR6), .EN(EN6), .O(O8));
  Asynchronous_One_Bit_Register asynchronous_one_bit_register_120 (.I(D8), .WR(WR7), .EN(EN7), .O(O8));
  Asynchronous_One_Bit_Register asynchronous_one_bit_register_121 (.I(D8), .WR(WR8), .EN(EN8), .O(O8));
  Asynchronous_One_Bit_Register asynchronous_one_bit_register_122 (.I(D8), .WR(WR9), .EN(EN9), .O(O8));
  Asynchronous_One_Bit_Register asynchronous_one_bit_register_123 (.I(D8), .WR(WR10), .EN(EN10), .O(O8));
  Asynchronous_One_Bit_Register asynchronous_one_bit_register_124 (.I(D8), .WR(WR11), .EN(EN11), .O(O8));
  Asynchronous_One_Bit_Register asynchronous_one_bit_register_125 (.I(D8), .WR(WR12), .EN(EN12), .O(O8));
  Asynchronous_One_Bit_Register asynchronous_one_bit_register_126 (.I(D8), .WR(WR13), .EN(EN13), .O(O8));
  Asynchronous_One_Bit_Register asynchronous_one_bit_register_127 (.I(D8), .WR(WR14), .EN(EN14), .O(O8));
  Asynchronous_One_Bit_Register asynchronous_one_bit_register_128 (.I(D8), .WR(WR15), .EN(EN15), .O(O8));
endmodule

module Static_RAM (
  input  D1,
  input  D2,
  input  D3,
  input  D4,
  input  D5,
  input  D6,
  input  D7,
  input  D8,
  input  WR,
  input  EN,
  input  A0,
  input  A1,
  input  A2,
  input  A3,
  output O1,
  output O2,
  output O3,
  output O4,
  output O5,
  output O6,
  output O7,
  output O8
);

  wire decoder_4_to_16_1_x0, decoder_4_to_16_1_x1, decoder_4_to_16_1_x2, decoder_4_to_16_1_x3,
       decoder_4_to_16_1_x4, decoder_4_to_16_1_x5, decoder_4_to_16_1_x6, decoder_4_to_16_1_x7,
       decoder_4_to_16_1_x8, decoder_4_to_16_1_x9, decoder_4_to_16_1_x10, decoder_4_to_16_1_x11,
       decoder_4_to_16_1_x12, decoder_4_to_16_1_x13, decoder_4_to_16_1_x14, decoder_4_to_16_1_x15,
       decoder_4_to_16_2_x0, decoder_4_to_16_2_x1, decoder_4_to_16_2_x2, decoder_4_to_16_2_x3,
       decoder_4_to_16_2_x4, decoder_4_to_16_2_x5, decoder_4_to_16_2_x6, decoder_4_to_16_2_x7,
       decoder_4_to_16_2_x8, decoder_4_to_16_2_x9, decoder_4_to_16_2_x10, decoder_4_to_16_2_x11,
       decoder_4_to_16_2_x12, decoder_4_to_16_2_x13, decoder_4_to_16_2_x14, decoder_4_to_16_2_x15, not_1_out,
       not_2_out;

  not not_1 (not_1_out, WR);
  not not_2 (not_2_out, EN);
  Decoder_4_to_16 decoder_4_to_16_1 (
    .S(not_1_out), .A0(A0), .A1(A1), .A2(A2), .A3(A3), .X0(decoder_4_to_16_1_x0), .X1(decoder_4_to_16_1_x1),
    .X2(decoder_4_to_16_1_x2), .X3(decoder_4_to_16_1_x3), .X4(decoder_4_to_16_1_x4),
    .X5(decoder_4_to_16_1_x5), .X6(decoder_4_to_16_1_x6), .X7(decoder_4_to_16_1_x7),
    .X8(decoder_4_to_16_1_x8), .X9(decoder_4_to_16_1_x9), .X10(decoder_4_to_16_1_x10),
    .X11(decoder_4_to_16_1_x11), .X12(decoder_4_to_16_1_x12), .X13(decoder_4_to_16_1_x13),
    .X14(decoder_4_to_16_1_x14), .X15(decoder_4_to_16_1_x15));
  Decoder_4_to_16 decoder_4_to_16_2 (
    .S(not_2_out), .A0(A0), .A1(A1), .A2(A2), .A3(A3), .X0(decoder_4_to_16_2_x0), .X1(decoder_4_to_16_2_x1),
    .X2(decoder_4_to_16_2_x2), .X3(decoder_4_to_16_2_x3), .X4(decoder_4_to_16_2_x4),
    .X5(decoder_4_to_16_2_x5), .X6(decoder_4_to_16_2_x6), .X7(decoder_4_to_16_2_x7),
    .X8(decoder_4_to_16_2_x8), .X9(decoder_4_to_16_2_x9), .X10(decoder_4_to_16_2_x10),
    .X11(decoder_4_to_16_2_x11), .X12(decoder_4_to_16_2_x12), .X13(decoder_4_to_16_2_x13),
    .X14(decoder_4_to_16_2_x14), .X15(decoder_4_to_16_2_x15));
  Static_RAM_16_Word_8_Bit_array static_ram_16_word_8_bit_array_1 (
    .D1(D1), .D2(D2), .D3(D3), .D4(D4), .D5(D5), .D6(D6), .D7(D7), .D8(D8), .WR0(decoder_4_to_16_1_x0),
    .EN0(decoder_4_to_16_2_x0), .WR1(decoder_4_to_16_1_x1), .EN1(decoder_4_to_16_2_x1),
    .WR2(decoder_4_to_16_1_x2), .EN2(decoder_4_to_16_2_x2), .WR3(decoder_4_to_16_1_x3),
    .EN3(decoder_4_to_16_2_x3), .WR4(decoder_4_to_16_1_x4), .EN4(decoder_4_to_16_2_x4),
    .WR5(decoder_4_to_16_1_x5), .EN5(decoder_4_to_16_2_x5), .WR6(decoder_4_to_16_1_x6),
    .EN6(decoder_4_to_16_2_x6), .WR7(decoder_4_to_16_1_x7), .EN7(decoder_4_to_16_2_x7),
    .WR8(decoder_4_to_16_1_x8), .EN8(decoder_4_to_16_2_x8), .WR9(decoder_4_to_16_1_x9),
    .EN9(decoder_4_to_16_2_x9), .WR10(decoder_4_to_16_1_x10), .EN10(decoder_4_to_16_2_x10),
    .WR11(decoder_4_to_16_1_x11), .EN11(decoder_4_to_16_2_x11), .WR12(decoder_4_to_16_1_x12),
    .EN12(decoder_4_to_16_2_x12), .WR13(decoder_4_to_16_1_x13), .EN13(decoder_4_to_16_2_x13),
    .WR14(decoder_4_to_16_1_x14), .EN14(decoder_4_to_16_2_x14), .WR15(decoder_4_to_16_1_x15),
    .EN15(decoder_4_to_16_2_x15), .O1(O1), .O2(O2), .O3(O3), .O4(O4), .O5(O5), .O6(O6), .O7(O7), .O8(O8));
endmodule

module Memory_Address_Register (
  input  Load,
  input  Clock,
  input  D1,
  input  D2,
  input  D3,
  input  D4,
  output A0,
  output A1,
  output A2,
  output A3
);

  One_Bit_Register one_bit_register_1 (.Load(Load), .Data(D1), .Clock(Clock), .O(A0));
  One_Bit_Register one_bit_register_2 (.Load(Load), .Data(D2), .Clock(Clock), .O(A1));
  One_Bit_Register one_bit_register_3 (.Load(Load), .Data(D3), .Clock(Clock), .O(A2));
  One_Bit_Register one_bit_register_4 (.Load(Load), .Data(D4), .Clock(Clock), .O(A3));
endmodule

module Multiplexer_2line_to_1line_4Bit (
  input  S,
  input  A0,
  input  A1,
  input  A2,
  input  A3,
  input  B0,
  input  B1,
  input  B2,
  input  B3,
  output O0,
  output O1,
  output O2,
  output O3
);

  wire and_1_out, and_2_out, and_3_out, and_4_out, and_5_out, and_6_out, and_7_out, and_8_out, not_1_out;

  not not_1 (not_1_out, S);
  and and_1 (and_1_out, A0, S);
  and and_2 (and_2_out, not_1_out, B0);
  and and_3 (and_3_out, A1, S);
  and and_4 (and_4_out, not_1_out, B1);
  and and_5 (and_5_out, A2, S);
  and and_6 (and_6_out, not_1_out, B2);
  and and_7 (and_7_out, A3, S);
  and and_8 (and_8_out, not_1_out, B3);
  or or_1 (O0, and_1_out, and_2_out);
  or or_2 (O1, and_3_out, and_4_out);
  or or_3 (O2, and_5_out, and_6_out);
  or or_4 (O3, and_7_out, and_8_out);
endmodule

module Multiplexer_2line_to_1line_8Bit (
  input  S,
  input  A0,
  input  A1,
  input  A2,
  input  A3,
  input  A4,
  input  A5,
  input  A6,
  input  A7,
  input  B0,
  input  B1,
  input  B2,
  input  B3,
  input  B4,
  input  B5,
  input  B6,
  input  B7,
  output O0,
  output O1,
  output O2,
  output O3,
  output O4,
  output O5,
  output O6,
  output O7
);

  wire and_1_out, and_2_out, and_3_out, and_4_out, and_5_out, and_6_out, and_7_out, and_8_out, and_9_out,
       and_10_out, and_11_out, and_12_out, and_13_out, and_14_out, and_15_out, and_16_out, not_1_out;

  not not_1 (not_1_out, S);
  and and_1 (and_1_out, A0, S);
  and and_2 (and_2_out, not_1_out, B0);
  and and_3 (and_3_out, A1, S);
  and and_4 (and_4_out, not_1_out, B1);
  and and_5 (and_5_out, A2, S);
  and and_6 (and_6_out, not_1_out, B2);
  and and_7 (and_7_out, A3, S);
  and and_8 (and_8_out, not_1_out, B3);
  and and_9 (and_9_out, A4, S);
  and and_10 (and_10_out, not_1_out, B4);
  and and_11 (and_11_out, A5, S);
  and and_12 (and_12_out, not_1_out, B5);
  and and_13 (and_13_out, A6, S);
  and and_14 (and_14_out, not_1_out, B6);
  and and_15 (and_15_out, A7, S);
  and and_16 (and_16_out, not_1_out, B7);
  or or_1 (O0, and_1_out, and_2_out);
  or or_2 (O1, and_3_out, and_4_out);
  or or_3 (O2, and_5_out, and_6_out);
  or or_4 (O3, and_7_out, and_8_out);
  or or_5 (O4, and_9_out, and_10_out);
  or or_6 (O5, and_11_out, and_12_out);
  or or_7 (O6, and_13_out, and_14_out);
  or or_8 (O7, and_15_out, and_16_out);
endmodule

module Master_Slave_JK_Latch (
  input  J,
  input  EN,
  input  K,
  output Q,
  output QC
);

  wire and_1_out, and_2_out, and_3_out, and_4_out, nor_1_out, nor_2_out, not_1_out;

  and and_1 (and_1_out, QC, J, EN);
  and and_2 (and_2_out, EN, K, Q);
  nor nor_1 (nor_1_out, and_1_out, nor_2_out);
  nor nor_2 (nor_2_out, nor_1_out, and_2_out);
  not not_1 (not_1_out, EN);
  and and_3 (and_3_out, nor_1_out, not_1_out);
  and and_4 (and_4_out, not_1_out, nor_2_out);
  nor nor_3 (Q, and_3_out, QC);
  nor nor_4 (QC, Q, and_4_out);
endmodule

module Binary_Counter (
  input  in_1,
  input  in_2,
  input  in_3,
  input  in_4,
  input  in_5,
  input  in_6,
  input  in_7,
  input  in_8,
  output out_9,
  output out_10,
  output out_11,
  output out_12
);

  wire clock_1_out;

  Clock clock_1 (.out(clock_1_out));
  J_K_Flip_Flop #(.trigger("falling")) j_k_ff_1 (
    .J(in_1), .K(in_2), .clk(clock_1_out), .Q(out_9));  // open: Qn, preset, reset
  J_K_Flip_Flop #(.trigger("falling")) j_k_ff_2 (
    .J(in_3), .K(in_4), .clk(out_9), .Q(out_10));  // open: Qn, preset, reset
  J_K_Flip_Flop #(.trigger("falling")) j_k_ff_3 (
    .J(in_5), .K(in_6), .clk(out_10), .Q(out_11));  // open: Qn, preset, reset
  J_K_Flip_Flop #(.trigger("falling")) j_k_ff_4 (
    .J(in_7), .K(in_8), .clk(out_11), .Q(out_12));  // open: Qn, preset, reset
endmodule

module Program_Counter (
  input  Count_Enable_CE,
  input  Clock,
  input  A,
  input  B,
  input  C,
  input  D,
  input  Jump_inverted,
  output O1,
  output O2,
  output O3,
  output O4
);

  wire n74161_1_pin1;

  _74161 u_74161_1 (
    .pin1(n74161_1_pin1), .pin2(Clock), .pin3(A), .pin4(B), .pin5(C), .pin6(D), .pin7(Count_Enable_CE),
    .pin14(O1), .pin13(O2), .pin12(O3), .pin11(O4), .pin10(Count_Enable_CE), .pin9(Jump_inverted));  // open: pin15
  // also tied to VCC on the sheet: n74161_1_pin1
endmodule

module Shift_Register (
  input  D,
  output out_2,
  output out_3,
  output out_4,
  output out_5,
  output out_6,
  output out_7,
  output out_8,
  output out_9
);

  wire clock_1_out;

  Clock clock_1 (.out(clock_1_out));
  D_Flip_Flop d_ff_1 (.D(D), .clk(clock_1_out), .Q(out_2));  // open: Qn, preset, reset
  D_Flip_Flop d_ff_2 (.D(out_2), .clk(clock_1_out), .Q(out_3));  // open: Qn, preset, reset
  D_Flip_Flop d_ff_3 (.D(out_3), .clk(clock_1_out), .Q(out_4));  // open: Qn, preset, reset
  D_Flip_Flop d_ff_4 (.D(out_4), .clk(clock_1_out), .Q(out_5));  // open: Qn, preset, reset
  D_Flip_Flop d_ff_5 (.D(out_5), .clk(clock_1_out), .Q(out_6));  // open: Qn, preset, reset
  D_Flip_Flop d_ff_6 (.D(out_6), .clk(clock_1_out), .Q(out_7));  // open: Qn, preset, reset
  D_Flip_Flop d_ff_7 (.D(out_7), .clk(clock_1_out), .Q(out_8));  // open: Qn, preset, reset
  D_Flip_Flop d_ff_8 (.D(out_8), .clk(clock_1_out), .Q(out_9));  // open: Qn, preset, reset
endmodule

module Decimal_Display (
  input  in_1,
  input  in_2,
  input  in_3,
  input  in_4,
  input  in_5,
  input  in_6,
  input  in_7,
  input  in_8
);

  wire [7:0] rom_1_data;

  ROM #(.misaligned("true")) rom_1 (.addr({in_8, in_7, in_6, in_5, in_4, in_3, in_2, in_1}), .data(rom_1_data));
  LED led_1 (.in(rom_1_data[0]));
  LED led_2 (.in(rom_1_data[1]));
  LED led_3 (.in(rom_1_data[2]));
  LED led_4 (.in(rom_1_data[3]));
  LED led_5 (.in(rom_1_data[4]));
  LED led_6 (.in(rom_1_data[5]));
  LED led_7 (.in(rom_1_data[6]));
  LED led_8 (.in(rom_1_data[7]));
  _7_Segment_Display u_7_segment_display_1 (
    .g(rom_1_data[0]), .f(rom_1_data[1]), .a(rom_1_data[6]), .b(rom_1_data[5]), .e(rom_1_data[2]),
    .d(rom_1_data[3]), .c(rom_1_data[4]), .dp(rom_1_data[7]));

  // Notes on the sheet:
  //   contents of rom_1 (hex, n*v repeats v):
  //   7e 30 6d 79 33 5b 5f 70 7f 7b 77 1f 4e 3d 4f 47 7e 30 6d 79 33 5b 5f 9*0 7e 30 6d 79 33 5b 5f 9*0 7e
  //   30 6d 79 33 5b 5f 70 8*0 7e 30 6d 79 33 5b 5f 70 8*0 7e 30 6d 79 33 5b 5f 70 8*0 7e 30 6d 79 33 5b
  //   5f 70 8*0 7e 30 6d 79 33 5b 5f 70 8*0 7e 30 6d 79 33 5b 5f 70 8*0 7e 30 6d 79 33 5b 5f 70 8*0 7e 30
  //   6d 79 33 5b 5f 70 8*0 7e 30 6d 79 33 5b 5f 70 8*0 7e 30 6d 79 33 5b 5f 70 8*0 7e 30 6d 79 33 5b 5f
  //   70 8*0 7e 30 6d 79 33 5b 5f 70 8*0 7e 30 6d 79 33 5b 5f 70
  //   g
  //   a
endmodule

module Seven_Seg_Driver (
  input  RBI,
  input  RNI,
  input  a,
  input  b,
  input  c,
  input  d,
  output A_2,
  output B_2,
  output C_2,
  output D_2,
  output E,
  output F,
  output G,
  output RBO,
  output RNO
);

  wire and_1_out, and_2_out, and_3_out, and_4_out, and_5_out, and_6_out, and_7_out, and_8_out, and_9_out,
       and_10_out, and_11_out, and_12_out, and_13_out, and_14_out, and_15_out, and_17_out, and_18_out,
       and_19_out, and_20_out, and_21_out, and_22_out, and_23_out, and_24_out, and_25_out, and_26_out,
       and_27_out, and_28_out, and_29_out, and_30_out, not_1_out, not_2_out, not_3_out, not_4_out, not_5_out,
       not_6_out, not_7_out, or_1_out, or_2_out, or_3_out, or_4_out, or_5_out, or_6_out, or_7_out, or_8_out,
       or_9_out, or_10_out, or_11_out, or_12_out, or_13_out, or_14_out, or_15_out, or_16_out, or_17_out,
       or_18_out, or_19_out, or_20_out, or_21_out;

  or or_1 (or_1_out, a, b);
  or or_2 (or_2_out, or_1_out, c);
  not not_1 (not_1_out, a);
  not not_2 (not_2_out, b);
  not not_3 (not_3_out, c);
  not not_4 (not_4_out, d);
  or or_3 (or_3_out, or_2_out, d);
  not not_5 (not_5_out, or_3_out);
  and and_1 (and_1_out, not_3_out, not_4_out);
  and and_2 (and_2_out, not_2_out, not_4_out);
  and and_3 (and_3_out, b, d);
  and and_4 (and_4_out, not_3_out, not_4_out);
  or or_4 (or_4_out, not_3_out, d);
  and and_5 (and_5_out, not_2_out, not_4_out);
  and and_6 (and_6_out, not_2_out, c);
  and and_7 (and_7_out, b, not_3_out);
  and and_8 (and_8_out, not_2_out, not_4_out);
  and and_9 (and_9_out, c, not_4_out);
  and and_10 (and_10_out, not_3_out, not_4_out);
  and and_11 (and_11_out, b, not_3_out);
  and and_12 (and_12_out, b, not_4_out);
  and and_13 (and_13_out, not_2_out, c);
  and and_14 (and_14_out, b, not_3_out);
  and and_15 (and_15_out, c, not_4_out);
  and and_16 (RBO, RBI, not_5_out);
  and and_17 (and_17_out, not_2_out, and_1_out);
  or or_5 (or_5_out, and_2_out, c);
  or or_6 (or_6_out, and_3_out, a);
  or or_7 (or_7_out, not_2_out, and_4_out);
  and and_18 (and_18_out, c, d);
  or or_8 (or_8_out, or_4_out, b);
  or or_9 (or_9_out, and_5_out, and_6_out);
  and and_19 (and_19_out, and_7_out, d);
  and and_20 (and_20_out, c, not_4_out);
  or or_10 (or_10_out, and_8_out, and_9_out);
  or or_11 (or_11_out, and_10_out, and_11_out);
  or or_12 (or_12_out, and_12_out, a);
  or or_13 (or_13_out, and_13_out, and_14_out);
  or or_14 (or_14_out, a, and_15_out);
  not not_6 (not_6_out, RBO);
  and and_21 (and_21_out, RNI, and_22_out);
  and and_22 (and_22_out, not_1_out, and_17_out);
  or or_15 (or_15_out, or_5_out, or_6_out);
  or or_16 (or_16_out, or_7_out, and_18_out);
  or or_17 (or_17_out, or_9_out, and_19_out);
  or or_18 (or_18_out, and_20_out, a);
  or or_19 (or_19_out, or_11_out, or_12_out);
  or or_20 (or_20_out, or_13_out, or_14_out);
  or or_21 (or_21_out, or_17_out, or_18_out);
  and and_23 (and_23_out, and_21_out, not_6_out);
  and and_24 (and_24_out, not_6_out, or_15_out);
  and and_25 (and_25_out, not_6_out, or_16_out);
  and and_26 (and_26_out, not_6_out, or_8_out);
  and and_27 (and_27_out, not_6_out, or_21_out);
  and and_28 (and_28_out, not_6_out, or_10_out);
  and and_29 (and_29_out, not_6_out, or_19_out);
  and and_30 (and_30_out, not_6_out, or_20_out);
  not not_7 (not_7_out, and_23_out);
  and and_31 (RNO, and_21_out, not_7_out);
  xor xor_1 (A_2, and_24_out, and_23_out);
  xor xor_2 (B_2, and_25_out, and_23_out);
  xor xor_3 (C_2, and_26_out, and_23_out);
  xor xor_4 (D_2, and_27_out, and_23_out);
  xor xor_5 (E, and_28_out, and_23_out);
  xor xor_6 (F, and_29_out, and_23_out);
  xor xor_7 (G, and_30_out, and_23_out);
  _7_Segment_Display u_7_segment_display_1 (.g(G), .f(F), .a(A_2), .b(B_2), .e(E), .d(D_2), .c(C_2));  // open: dp

  // Notes on the sheet:
  //   Ripple Blinking
  //   Negative sign
endmodule

module Dabble (
  input  in_1,
  input  in_2,
  input  in_3,
  input  in_4,
  output out_5,
  output out_6,
  output out_7,
  output out_8
);

  wire and_1_out, and_2_out, and_3_out, and_4_out, and_5_out, and_6_out, and_7_out, and_8_out, and_9_out,
       and_10_out, and_11_out, and_12_out, and_13_out, not_1_out, not_2_out, not_3_out, not_4_out, or_1_out,
       or_2_out, or_6_out;

  not not_1 (not_1_out, in_1);
  not not_2 (not_2_out, in_2);
  not not_3 (not_3_out, in_3);
  not not_4 (not_4_out, in_4);
  and and_1 (and_1_out, in_2, in_4);
  and and_2 (and_2_out, in_2, in_3);
  and and_3 (and_3_out, in_2, not_3_out);
  and and_4 (and_4_out, not_2_out, in_3);
  and and_5 (and_5_out, in_3, in_4);
  and and_6 (and_6_out, not_1_out, not_2_out);
  and and_7 (and_7_out, in_2, in_3);
  or or_1 (or_1_out, and_1_out, and_2_out);
  and and_8 (and_8_out, and_3_out, not_4_out);
  and and_9 (and_9_out, in_1, in_4);
  or or_2 (or_2_out, and_4_out, and_5_out);
  and and_10 (and_10_out, in_1, not_4_out);
  and and_11 (and_11_out, and_6_out, in_4);
  and and_12 (and_12_out, and_7_out, not_4_out);
  or or_3 (out_5, or_1_out, in_1);
  or or_4 (out_6, and_8_out, and_9_out);
  or or_5 (out_7, or_2_out, and_10_out);
  or or_6 (or_6_out, and_11_out, and_12_out);
  or or_7 (out_8, or_6_out, and_13_out);
  and and_13 (and_13_out, in_1, not_4_out);
endmodule

module Double_Dabble (
  input  a,
  input  b,
  input  c,
  input  d,
  input  e,
  input  f,
  input  g,
  input  h,
  output H_3,
  output H_2,
  output H_1,
  output H_0,
  output T_3,
  output T_2,
  output T_1,
  output T_0,
  output O_3,
  output O_2,
  output O_1,
  output O_0
);

  wire T_out_5, T_out_6, T_out_7, T_out_8, U_out_5, U_out_6, U_out_7, U_out_8, V_out_5, V_out_6, V_out_7,
       V_out_8, W_out_6, W_out_7, W_out_8, X_out_5, X_out_6, X_out_7, X_out_8;

  Dabble T (
    .in_2(a), .in_3(b), .in_4(c), .out_5(T_out_5), .out_6(T_out_6), .out_7(T_out_7), .out_8(T_out_8));  // open: in_1
  Dabble U (
    .in_1(T_out_6), .in_2(T_out_7), .in_3(T_out_8), .in_4(d), .out_5(U_out_5), .out_6(U_out_6),
    .out_7(U_out_7), .out_8(U_out_8));
  Dabble V (
    .in_1(U_out_6), .in_2(U_out_7), .in_3(U_out_8), .in_4(e), .out_5(V_out_5), .out_6(V_out_6),
    .out_7(V_out_7), .out_8(V_out_8));
  Dabble W (
    .in_2(T_out_5), .in_3(U_out_5), .in_4(V_out_5), .out_5(H_1), .out_6(W_out_6), .out_7(W_out_7),
    .out_8(W_out_8));  // open: in_1
  Dabble X (
    .in_1(V_out_6), .in_2(V_out_7), .in_3(V_out_8), .in_4(f), .out_5(X_out_5), .out_6(X_out_6),
    .out_7(X_out_7), .out_8(X_out_8));
  Dabble Y (
    .in_1(W_out_6), .in_2(W_out_7), .in_3(W_out_8), .in_4(X_out_5), .out_5(H_0), .out_6(T_3), .out_7(T_2),
    .out_8(T_1));
  Dabble Z (
    .in_1(X_out_6), .in_2(X_out_7), .in_3(X_out_8), .in_4(g), .out_5(T_0), .out_6(O_3), .out_7(O_2),
    .out_8(O_1));

  assign O_0 = h;
endmodule

module Negate (
  input  Enable,
  input  a,
  input  b,
  input  c,
  input  d,
  input  e,
  input  f,
  input  g,
  input  h,
  output out_10,
  output out_11,
  output out_12,
  output out_13,
  output out_14,
  output out_15,
  output out_16,
  output out_17
);

  wire xor_1_out, xor_2_out, xor_3_out, xor_4_out, xor_5_out, xor_6_out, xor_7_out, xor_8_out;

  xor xor_1 (xor_1_out, a, Enable);
  xor xor_2 (xor_2_out, b, Enable);
  xor xor_3 (xor_3_out, c, Enable);
  xor xor_4 (xor_4_out, d, Enable);
  xor xor_5 (xor_5_out, e, Enable);
  xor xor_6 (xor_6_out, f, Enable);
  xor xor_7 (xor_7_out, g, Enable);
  xor xor_8 (xor_8_out, h, Enable);
  Eight_Bit_Adder eight_bit_adder_1 (
    .A1(xor_1_out), .A2(xor_2_out), .A3(xor_3_out), .A4(xor_4_out), .A5(xor_5_out), .A6(xor_6_out),
    .A7(xor_7_out), .A8(xor_8_out), .Cin(Enable), .S1(out_10), .S2(out_11), .S3(out_12), .S4(out_13),
    .S5(out_14), .S6(out_15), .S7(out_16), .S8(out_17));  // open: B1, B2, B3, B4, B5, B6, B7, B8, Cout
endmodule

module Display (
  input  RB,
  input  TwoS_Complement,
  input  D8,
  input  D7,
  input  D6,
  input  D5,
  input  D4,
  input  D3,
  input  D2,
  input  D1,
  output out_11,
  output out_12,
  output out_13,
  output out_14,
  output out_15,
  output out_16,
  output out_17,
  output out_18,
  output out_19,
  output out_20,
  output out_21,
  output out_22,
  output out_23,
  output out_24,
  output out_25,
  output out_26,
  output out_27,
  output out_28,
  output out_29,
  output out_30,
  output out_31,
  output out_32,
  output out_33,
  output out_34,
  output out_35,
  output out_36,
  output out_37,
  output out_38
);

  wire and_1_out, and_2_out, double_dabble_1_h_0, double_dabble_1_h_1, double_dabble_1_h_2,
       double_dabble_1_h_3, double_dabble_1_o_0, double_dabble_1_o_1, double_dabble_1_o_2,
       double_dabble_1_o_3, double_dabble_1_t_0, double_dabble_1_t_1, double_dabble_1_t_2,
       double_dabble_1_t_3, negate_1_out_10, negate_1_out_11, negate_1_out_12, negate_1_out_13,
       negate_1_out_14, negate_1_out_15, negate_1_out_16, negate_1_out_17, not_1_out, seven_seg_driver_1_rbo,
       seven_seg_driver_1_rno, seven_seg_driver_2_rbo, seven_seg_driver_2_rno;

  and and_1 (and_1_out, TwoS_Complement, D8);
  and and_2 (and_2_out, RB, not_1_out);
  not not_1 (not_1_out, and_1_out);
  Negate negate_1 (
    .Enable(and_1_out), .a(D8), .b(D7), .c(D6), .d(D5), .e(D4), .f(D3), .g(D2), .h(D1),
    .out_10(negate_1_out_10), .out_11(negate_1_out_11), .out_12(negate_1_out_12), .out_13(negate_1_out_13),
    .out_14(negate_1_out_14), .out_15(negate_1_out_15), .out_16(negate_1_out_16), .out_17(negate_1_out_17));
  Double_Dabble double_dabble_1 (
    .a(negate_1_out_10), .b(negate_1_out_11), .c(negate_1_out_12), .d(negate_1_out_13), .e(negate_1_out_14),
    .f(negate_1_out_15), .g(negate_1_out_16), .h(negate_1_out_17), .H_3(double_dabble_1_h_3),
    .H_2(double_dabble_1_h_2), .H_1(double_dabble_1_h_1), .H_0(double_dabble_1_h_0),
    .T_3(double_dabble_1_t_3), .T_2(double_dabble_1_t_2), .T_1(double_dabble_1_t_1),
    .T_0(double_dabble_1_t_0), .O_3(double_dabble_1_o_3), .O_2(double_dabble_1_o_2),
    .O_1(double_dabble_1_o_1), .O_0(double_dabble_1_o_0));
  Seven_Seg_Driver seven_seg_driver_1 (
    .RBI(and_2_out), .RNI(and_1_out), .A_2(out_11), .B_2(out_12), .C_2(out_13), .D_2(out_14), .E(out_15),
    .F(out_16), .G(out_17), .RBO(seven_seg_driver_1_rbo), .RNO(seven_seg_driver_1_rno));  // open: a, b, c, d
  Seven_Seg_Driver seven_seg_driver_2 (
    .RBI(seven_seg_driver_1_rbo), .RNI(seven_seg_driver_1_rno), .a(double_dabble_1_h_3),
    .b(double_dabble_1_h_2), .c(double_dabble_1_h_1), .d(double_dabble_1_h_0), .A_2(out_18), .B_2(out_19),
    .C_2(out_20), .D_2(out_21), .E(out_22), .F(out_23), .G(out_24), .RBO(seven_seg_driver_2_rbo),
    .RNO(seven_seg_driver_2_rno));
  Seven_Seg_Driver seven_seg_driver_3 (
    .RBI(seven_seg_driver_2_rbo), .RNI(seven_seg_driver_2_rno), .a(double_dabble_1_t_3),
    .b(double_dabble_1_t_2), .c(double_dabble_1_t_1), .d(double_dabble_1_t_0), .A_2(out_25), .B_2(out_26),
    .C_2(out_27), .D_2(out_28), .E(out_29), .F(out_30), .G(out_31));  // open: RBO, RNO
  Seven_Seg_Driver seven_seg_driver_4 (
    .a(double_dabble_1_o_3), .b(double_dabble_1_o_2), .c(double_dabble_1_o_1), .d(double_dabble_1_o_0),
    .A_2(out_32), .B_2(out_33), .C_2(out_34), .D_2(out_35), .E(out_36), .F(out_37), .G(out_38));  // open: RBI, RNI, RBO, RNO
endmodule

module Output_Register (
  input  Clock,
  input  Control,
  input  D1,
  input  D2,
  input  D3,
  input  D4,
  input  D5,
  input  D6,
  input  D7,
  input  D8,
  output O8,
  output O7,
  output O6,
  output O5,
  output O4,
  output O3,
  output O2,
  output O1
);

  wire and_1_out, n74273_1_pin1;

  and and_1 (and_1_out, Clock, Control);
  _74273 u_74273_1 (
    .pin1(n74273_1_pin1), .pin2(O1), .pin3(D1), .pin4(D2), .pin5(O2), .pin6(O3), .pin7(D3), .pin8(D4),
    .pin9(O4), .pin19(O8), .pin18(D8), .pin17(D7), .pin16(O7), .pin15(O6), .pin14(D6), .pin13(D5),
    .pin12(O5), .pin11(and_1_out));
  // also tied to VCC on the sheet: n74273_1_pin1
endmodule
